// Logisim project 2-bit Full Adder.circ as structural Verilog: 2 circuits, main circuit main
module main (
  input  [1:0] A,
  input  in_2,
  input  [1:0] in_3,
  output carry,
  output SUM,
  output out_6
);

  wire adder_2_cout;

  Adder #(.width(1)) adder_1 (.a(A[1]), .b(in_3[1]), .out(SUM), .cin(adder_2_cout), .cout(carry));
  Adder #(.width(1)) adder_2 (.a(A[0]), .b(in_3[0]), .out(out_6), .cin(in_2), .cout(adder_2_cout));

  // Notes on the sheet:
  //   B
endmodule

module _8_bit_adder (
  input  in_1,
  input  [3:0] A,
  input  [3:0] B,
  input  in_4,
  input  in_5,
  input  in_6,
  input  in_7,
  input  [1:0] Selection,
  input  in_9,
  input  in_10,
  input  in_11,
  output carry,
  output [3:0] SUM,
  output out_14,
  output out_15
);

  Adder #(.width(4)) adder_1 (.a(A), .b(B), .out(SUM), .cin(in_1), .cout(carry));
  Multiplexer #(.enable("false")) multiplexer_1 (.in0(in_9), .in1(in_10), .out(out_15), .sel(in_11));
  Multiplexer #(.select(2), .enable("false")) multiplexer_2 (
    .in0(in_4), .in1(in_5), .in2(in_6), .in3(in_7), .out(out_14), .sel(Selection));
endmodule
