// Logisim project ex02.circ as structural Verilog: 4 circuits, main circuit 8-bit adder
// 1-bit
module _1_bit_full_adder (
  input  A,
  input  B,
  input  Cin,
  output Cout,
  output S
);

  wire and_1_out, and_2_out, and_3_out, and_4_out, and_5_out, and_6_out, and_7_out, and_8_out, and_9_out,
       and_10_out, and_11_out, not_1_out, not_2_out, not_3_out, not_4_out, not_5_out, not_6_out, or_1_out,
       or_3_out, or_4_out;

  and and_1 (and_1_out, B, Cin);
  and and_2 (and_2_out, A, Cin);
  not not_1 (not_1_out, A);
  not not_2 (not_2_out, B);
  not not_3 (not_3_out, A);
  not not_4 (not_4_out, B);
  or or_1 (or_1_out, and_1_out, and_2_out);
  and and_3 (and_3_out, A, B);
  and and_4 (and_4_out, not_1_out, not_2_out);
  and and_5 (and_5_out, not_3_out, B);
  not not_5 (not_5_out, Cin);
  and and_6 (and_6_out, A, not_4_out);
  not not_6 (not_6_out, Cin);
  and and_7 (and_7_out, A, B);
  or or_2 (Cout, or_1_out, and_3_out);
  and and_8 (and_8_out, and_4_out, Cin);
  and and_9 (and_9_out, and_5_out, not_5_out);
  and and_10 (and_10_out, and_6_out, not_6_out);
  and and_11 (and_11_out, and_7_out, Cin);
  or or_3 (or_3_out, and_8_out, and_9_out);
  or or_4 (or_4_out, and_10_out, and_11_out);
  or or_5 (S, or_3_out, or_4_out);
endmodule

// 2-bit
module _2_bit_full_adder (
  input  Cin,
  input  [1:0] A,
  input  [1:0] B,
  output [1:0] SUM,
  output Cout
);

  wire _0_cout;

  _1_bit_full_adder _0 (.A(A[0]), .B(B[0]), .Cin(Cin), .Cout(_0_cout), .S(SUM[0]));
  _1_bit_full_adder _1 (.A(A[1]), .B(B[1]), .Cin(_0_cout), .Cout(Cout), .S(SUM[1]));
endmodule

// 4-bit
module _4_bit_full_adder (
  input  Cin,
  input  [3:0] A,
  input  [3:0] B,
  output [3:0] Sum,
  output Cout
);

  wire n2_bit_full_adder_1_cout;

  _2_bit_full_adder u_2_bit_full_adder_1 (
    .A(A[1:0]), .B(B[1:0]), .SUM(Sum[1:0]), .Cin(Cin), .Cout(n2_bit_full_adder_1_cout));
  _2_bit_full_adder u_2_bit_full_adder_2 (
    .A(A[3:2]), .B(B[3:2]), .SUM(Sum[3:2]), .Cin(n2_bit_full_adder_1_cout), .Cout(Cout));
endmodule

module _8_bit_adder (
  input  Cin,
  input  [7:0] A,
  input  [7:0] B,
  output [7:0] SUM,
  output Cout
);

  wire n4_bit_full_adder_1_cout;

  _4_bit_full_adder u_4_bit_full_adder_1 (
    .A(A[3:0]), .B(B[3:0]), .Sum(SUM[3:0]), .Cin(Cin), .Cout(n4_bit_full_adder_1_cout));
  _4_bit_full_adder u_4_bit_full_adder_2 (
    .A(A[7:4]), .B(B[7:4]), .Sum(SUM[7:4]), .Cin(n4_bit_full_adder_1_cout), .Cout(Cout));
endmodule
