// Logisim project ex03.circ as structural Verilog: 3 circuits, main circuit main
module main (
  input  [7:0] \input 
);

  wire [3:0] binarytobcd_1_hundred, binarytobcd_1_single, binarytobcd_1_ten, Valid_BCD_2_out_2,
       Valid_BCD_3_out_2, Valid_BCD_out_2;
  wire [7:0] multiplexer_1_out, n8_bit_adder_1_sum, not_1_out;

  assign not_1_out = ~\input ;  // NOT_Gate not_1, 8 bits wide
  _8_bit_adder u_8_bit_adder_1 (.A(8'h1), .B(not_1_out), .SUM(n8_bit_adder_1_sum), .Cin(1'b0));  // open: Cout
  Multiplexer #(.width(8), .enable("false")) multiplexer_1 (
    .in0(\input ), .in1(n8_bit_adder_1_sum), .out(multiplexer_1_out), .sel(\input [7]));
  _7_Segment_Display u_7_segment_display_1 (.g(\input [7]));  // open: f, a, b, e, d, c, dp
  Hex_Digit_Display hex_digit_display_1 (.value(Valid_BCD_out_2));  // open: dp
  ValidBCD Valid_BCD (.in_1(binarytobcd_1_hundred), .out_2(Valid_BCD_out_2));
  binaryToBCD binarytobcd_1 (
    .\input (multiplexer_1_out), .hundred(binarytobcd_1_hundred), .ten(binarytobcd_1_ten),
    .single(binarytobcd_1_single));
  Hex_Digit_Display hex_digit_display_2 (.value(Valid_BCD_3_out_2));  // open: dp
  Hex_Digit_Display hex_digit_display_3 (.value(Valid_BCD_2_out_2));  // open: dp
  ValidBCD Valid_BCD_2 (.in_1(binarytobcd_1_ten), .out_2(Valid_BCD_2_out_2));
  ValidBCD Valid_BCD_3 (.in_1(binarytobcd_1_single), .out_2(Valid_BCD_3_out_2));
endmodule

// BCD
module binaryToBCD (
  input  [7:0] \input ,
  output [3:0] hundred,
  output [3:0] ten,
  output [3:0] single
);

  wire [7:0] divider_1_rem;
  wire [7:4] divider_1_out, divider_2_out, divider_2_rem;

  Divider divider_1 (.a(\input ), .b(8'h64), .out({divider_1_out, hundred}), .upper({8{1'b0}}), .rem(divider_1_rem));
  Divider divider_2 (
    .a(divider_1_rem), .b(8'ha), .out({divider_2_out, ten}), .upper({8{1'b0}}), .rem({divider_2_rem, single}));
endmodule

module ValidBCD (
  input  [3:0] in_1,
  output [3:0] out_2
);

  wire and_1_out, and_2_out, or_1_out;

  and and_1 (and_1_out, in_1[1], in_1[3]);
  and and_2 (and_2_out, in_1[2], in_1[3]);
  or or_1 (or_1_out, and_1_out, and_2_out);
  Hex_Digit_Display hex_digit_display_1 (.value(out_2));  // open: dp
  Multiplexer #(.width(4), .enable("false")) multiplexer_1 (.in0(in_1), .out(out_2), .sel(or_1_out));  // open: in1
endmodule
