// Logisim project ex04.circ as structural Verilog: 2 circuits, main circuit main
module main (
  input  [7:0] \input ,
  output [3:0] Hex
);

  mybit_bit_adder mybit_bit_adder_1 (.\input (\input ), .Hex(Hex));
endmodule

module mybit_bit_adder (
  input  [7:0] \input ,
  output [3:0] Hex
);

  wire and_1_out, and_2_out, and_3_out, and_4_out, or_1_out, or_2_out, or_3_out, or_4_out;
  wire [1:0] adder_1_out, adder_2_out, adder_3_out, adder_4_out, adder_5_out, adder_6_out;
  wire [2:2] adder_5_cout, adder_6_cout;

  and and_1 (and_1_out, \input [0], \input [1]);
  or or_1 (or_1_out, \input [0], \input [1]);
  or or_2 (or_2_out, \input [2], \input [3]);
  and and_2 (and_2_out, \input [2], \input [3]);
  and and_3 (and_3_out, \input [4], \input [5]);
  or or_3 (or_3_out, \input [4], \input [5]);
  or or_4 (or_4_out, \input [6], \input [7]);
  and and_4 (and_4_out, \input [6], \input [7]);
  Adder #(.width(1)) adder_1 (.a(and_1_out), .b(or_1_out), .out(adder_1_out[0]), .cout(adder_1_out[1]));  // open: cin
  Adder #(.width(1)) adder_2 (.a(or_2_out), .b(and_2_out), .out(adder_2_out[0]), .cout(adder_2_out[1]));  // open: cin
  Adder #(.width(1)) adder_3 (.a(and_3_out), .b(or_3_out), .out(adder_3_out[0]), .cout(adder_3_out[1]));  // open: cin
  Adder #(.width(1)) adder_4 (.a(or_4_out), .b(and_4_out), .out(adder_4_out[0]), .cout(adder_4_out[1]));  // open: cin
  Adder #(.width(2)) adder_5 (
    .a(adder_1_out), .b(adder_2_out), .out(adder_5_out), .cout(adder_5_cout[2]));  // open: cin
  Adder #(.width(2)) adder_6 (
    .a(adder_3_out), .b(adder_4_out), .out(adder_6_out), .cout(adder_6_cout[2]));  // open: cin
  Adder #(.width(3)) adder_7 (
    .a({adder_5_cout[2], adder_5_out}), .b({adder_6_cout[2], adder_6_out}), .out(Hex[2:0]), .cout(Hex[3]));  // open: cin
endmodule
