// Logisim project ex05.circ as structural Verilog: 5 circuits, main circuit main
module main (
  input  [15:0] input_A,
  input  [15:0] input_B
);

  wire n4_bit_bcd_adder_1_cout;
  wire [3:0] bit_extender_1_out, n4_bit_bcd_adder_1_sum, n4_bit_bcd_adder_1_sum_2, n4_bit_bcd_adder_1_sum_3,
       n4_bit_bcd_adder_1_sum_4;

  Hex_Digit_Display hex_digit_display_1 (.value(input_A[15:12]));  // open: dp
  Hex_Digit_Display hex_digit_display_2 (.value(input_A[11:8]));  // open: dp
  Hex_Digit_Display hex_digit_display_3 (.value(input_A[7:4]));  // open: dp
  Hex_Digit_Display hex_digit_display_4 (.value(input_A[3:0]));  // open: dp
  Hex_Digit_Display hex_digit_display_5 (.value(input_B[15:12]));  // open: dp
  _4_bit_BCD_adder u_4_bit_bcd_adder_1 (
    .input_A(input_A), .input_A_2(input_B),
    .SUM({n4_bit_bcd_adder_1_sum_4, n4_bit_bcd_adder_1_sum_3, n4_bit_bcd_adder_1_sum_2, n4_bit_bcd_adder_1_sum}),
    .Cout(n4_bit_bcd_adder_1_cout));
  Hex_Digit_Display hex_digit_display_6 (.value(input_B[11:8]));  // open: dp
  Hex_Digit_Display hex_digit_display_7 (.value(input_B[7:4]));  // open: dp
  Hex_Digit_Display hex_digit_display_8 (.value(input_B[3:0]));  // open: dp
  assign bit_extender_1_out = {{3{1'b0}}, n4_bit_bcd_adder_1_cout};  // Bit_Extender bit_extender_1
  Hex_Digit_Display hex_digit_display_9 (.value(bit_extender_1_out));  // open: dp
  Hex_Digit_Display hex_digit_display_10 (.value(n4_bit_bcd_adder_1_sum_4));  // open: dp
  Hex_Digit_Display hex_digit_display_11 (.value(n4_bit_bcd_adder_1_sum_3));  // open: dp
  Hex_Digit_Display hex_digit_display_12 (.value(n4_bit_bcd_adder_1_sum));  // open: dp
  Hex_Digit_Display hex_digit_display_13 (.value(n4_bit_bcd_adder_1_sum_2));  // open: dp

  // Notes on the sheet:
  //   +
  //   =
endmodule

module _4_bit_BCD_adder (
  input  [15:0] input_A,
  input  [15:0] input_A_2,
  output Cout,
  output [15:0] SUM
);

  wire my2bit_bcd_adder_1_cout;
  wire [3:0] bit_extender_1_out;

  Hex_Digit_Display hex_digit_display_1 (.value(input_A[15:12]));  // open: dp
  Hex_Digit_Display hex_digit_display_2 (.value(input_A_2[11:8]));  // open: dp
  Hex_Digit_Display hex_digit_display_3 (.value(input_A_2[15:12]));  // open: dp
  Hex_Digit_Display hex_digit_display_4 (.value(input_A[7:4]));  // open: dp
  Hex_Digit_Display hex_digit_display_5 (.value(input_A[11:8]));  // open: dp
  Hex_Digit_Display hex_digit_display_6 (.value(input_A_2[7:4]));  // open: dp
  Hex_Digit_Display hex_digit_display_7 (.value(input_A_2[3:0]));  // open: dp
  Hex_Digit_Display hex_digit_display_8 (.value(input_A[3:0]));  // open: dp
  my2bit_BCD_adder my2bit_bcd_adder_1 (
    .Input_A(input_A[7:0]), .Input_B(input_A_2[7:0]), .Cout(my2bit_bcd_adder_1_cout), .Sum(SUM[7:0]),
    .Cin(1'b0));
  my2bit_BCD_adder my2bit_bcd_adder_2 (
    .Input_A(input_A[15:8]), .Input_B(input_A_2[15:8]), .Cout(Cout), .Sum(SUM[15:8]),
    .Cin(my2bit_bcd_adder_1_cout));
  assign bit_extender_1_out = {{3{1'b0}}, Cout};  // Bit_Extender bit_extender_1
  Hex_Digit_Display hex_digit_display_9 (.value(SUM[15:12]));  // open: dp
  Hex_Digit_Display hex_digit_display_10 (.value(bit_extender_1_out));  // open: dp
  Hex_Digit_Display hex_digit_display_11 (.value(SUM[11:8]));  // open: dp
  Hex_Digit_Display hex_digit_display_12 (.value(SUM[7:4]));  // open: dp
  Hex_Digit_Display hex_digit_display_13 (.value(SUM[3:0]));  // open: dp
endmodule

module _1_bit_BCD_adder (
  input  [3:0] Input_A,
  input  Cin,
  input  [3:0] Input_B,
  output Cout,
  output [3:0] Sum
);

  wire adder_1_cout;
  wire [3:0] adder_1_out;

  Hex_Digit_Display hex_digit_display_1 (.value(Input_A));  // open: dp
  Hex_Digit_Display hex_digit_display_2 (.value(Input_B));  // open: dp
  Adder #(.width(4)) adder_1 (.a(Input_A), .b(Input_B), .out(adder_1_out), .cin(Cin), .cout(adder_1_cout));
  binary_to_BCD binary_to_bcd_1 (
    .E(adder_1_cout), .D(adder_1_out[3]), .C(adder_1_out[2]), .B(adder_1_out[1]), .A(adder_1_out[0]),
    .a4(Cout), .a3(Sum[3]), .a2(Sum[2]), .a1(Sum[1]), .a0(Sum[0]));
  _7_Segment_Display u_7_segment_display_1 (.b(Cout), .c(Cout));  // open: g, f, a, e, d, dp
  Hex_Digit_Display hex_digit_display_3 (.value(Sum));  // open: dp
endmodule

module binary_to_BCD (
  input  E,
  input  D,
  input  C,
  input  B,
  input  A,
  output a4,
  output a3,
  output a2,
  output a1,
  output a0
);

  wire and_1_out, and_2_out, and_3_out, and_4_out, and_5_out, and_6_out, and_7_out, and_8_out, and_9_out,
       and_10_out, and_11_out, and_12_out, and_13_out, and_14_out, and_15_out, and_16_out, not_1_out,
       not_2_out, not_3_out, not_4_out, not_5_out, not_6_out, not_7_out, not_8_out, not_9_out, or_1_out,
       or_4_out, or_6_out, or_7_out;

  and and_1 (and_1_out, D, B);
  and and_2 (and_2_out, D, C);
  not not_1 (not_1_out, C);
  not not_2 (not_2_out, D);
  not not_3 (not_3_out, E);
  not not_4 (not_4_out, D);
  not not_5 (not_5_out, C);
  or or_1 (or_1_out, and_1_out, and_2_out);
  and and_3 (and_3_out, D, not_1_out);
  not not_6 (not_6_out, B);
  and and_4 (and_4_out, not_2_out, C);
  and and_5 (and_5_out, C, B);
  not not_7 (not_7_out, B);
  and and_6 (and_6_out, not_3_out, not_4_out);
  and and_7 (and_7_out, D, C);
  not not_8 (not_8_out, B);
  and and_8 (and_8_out, not_5_out, A);
  and and_9 (and_9_out, B, A);
  or or_2 (a4, or_1_out, E);
  and and_10 (and_10_out, and_3_out, not_6_out);
  or or_3 (a3, and_10_out, and_11_out);
  and and_11 (and_11_out, E, B);
  or or_4 (or_4_out, and_4_out, and_5_out);
  or or_5 (a2, or_4_out, and_12_out);
  and and_12 (and_12_out, E, not_7_out);
  and and_13 (and_13_out, and_6_out, B);
  or or_6 (or_6_out, and_13_out, and_14_out);
  and and_14 (and_14_out, and_7_out, not_8_out);
  and and_15 (and_15_out, E, not_9_out);
  not not_9 (not_9_out, B);
  or or_7 (or_7_out, and_8_out, and_9_out);
  or or_8 (a0, or_7_out, and_16_out);
  and and_16 (and_16_out, D, A);
  or or_9 (a1, or_6_out, and_15_out);
endmodule

module my2bit_BCD_adder (
  input  Cin,
  input  [7:0] Input_A,
  input  [7:0] Input_B,
  output Cout,
  output [7:0] Sum
);

  wire n1_bit_bcd_adder_1_cout;
  wire [3:0] bit_extender_1_out;

  Hex_Digit_Display hex_digit_display_1 (.value(Input_B[7:4]));  // open: dp
  Hex_Digit_Display hex_digit_display_2 (.value(Input_A[3:0]));  // open: dp
  Hex_Digit_Display hex_digit_display_3 (.value(Input_A[7:4]));  // open: dp
  Hex_Digit_Display hex_digit_display_4 (.value(Input_B[3:0]));  // open: dp
  _1_bit_BCD_adder u_1_bit_bcd_adder_1 (
    .Input_A(Input_A[3:0]), .Input_B(Input_B[3:0]), .Cout(n1_bit_bcd_adder_1_cout), .Sum(Sum[3:0]), .Cin(Cin));
  _1_bit_BCD_adder u_1_bit_bcd_adder_2 (
    .Input_A(Input_A[7:4]), .Input_B(Input_B[7:4]), .Cout(Cout), .Sum(Sum[7:4]), .Cin(n1_bit_bcd_adder_1_cout));
  assign bit_extender_1_out = {{3{1'b0}}, Cout};  // Bit_Extender bit_extender_1
  Hex_Digit_Display hex_digit_display_5 (.value(bit_extender_1_out));  // open: dp
  Hex_Digit_Display hex_digit_display_6 (.value(Sum[7:4]));  // open: dp
  Hex_Digit_Display hex_digit_display_7 (.value(Sum[3:0]));  // open: dp
endmodule
