// Logisim project MyCPU.circ as structural Verilog: 8 circuits, main circuit main
module main (
  input  in_1,
  input  in_2,
  input  C_MAR,
  input  in_4,
  input  in_5,
  input  in_6,
  input  C_MBR,
  input  C_D0,
  input  in_9,
  input  in_10,
  input  in_11,
  input  C_IR,
  input  OPERAND0_3,
  output z
);

  wire h2bcd_1_sign;
  wire [2:0] IR_q_2, subtractor_1_out;
  wire [3:0] adder_1_out, controlled_buffer_1_out, h2bcd_1_hundred, h2bcd_1_single, h2bcd_1_ten, MAR_q,
       multiplexer_1_out, PC_q;
  wire [7:0] controlled_buffer_2_out, D0_q, IR_q, MBR_q, ram_1_data;

  Adder #(.width(4)) adder_1 (.a(PC_q), .b(4'b0001), .out(adder_1_out));  // open: cin, cout
  Multiplexer #(.width(4), .enable("false")) multiplexer_1 (
    .in0(controlled_buffer_1_out), .in1(adder_1_out), .out(multiplexer_1_out), .sel(in_1));
  Register #(.width(4)) PC (.D(multiplexer_1_out), .Q(PC_q), .clk(in_2));  // open: en, clr
  assign controlled_buffer_1_out = C_MAR ? PC_q : 4'bz;  // Controlled_Buffer controlled_buffer_1
  Register #(.width(4), .trigger("high")) MAR (.D(controlled_buffer_1_out), .Q(MAR_q), .clk(in_4));  // open: en, clr
  assign controlled_buffer_2_out = in_6 ? ram_1_data : 8'bz;  // Controlled_Buffer controlled_buffer_2
  RAM #(.addrWidth(4), .bus("separate")) ram_1 (
    .addr(MAR_q), .din(controlled_buffer_2_out), .data(ram_1_data), .clk(in_5));  // open: str, sel, ld, clr
  Register #(.trigger("high")) MBR (.D(controlled_buffer_2_out), .Q(MBR_q), .clk(C_MBR));  // open: en, clr
  Register #(.trigger("high")) D0 (.D(controlled_buffer_2_out), .Q(D0_q), .clk(C_D0));  // open: en, clr
  Register #(.trigger("high")) IR (
    .D(controlled_buffer_2_out), .Q({IR_q[7], IR_q_2, IR_q[3:0]}), .clk(C_IR));  // open: en, clr
  _7_Segment_Display u_7_segment_display_1 (.g(h2bcd_1_sign));  // open: f, a, b, e, d, c, dp
  assign controlled_buffer_2_out = in_9 ? D0_q : 8'bz;  // Controlled_Buffer controlled_buffer_3
  assign controlled_buffer_1_out = OPERAND0_3 ? IR_q[3:0] : 4'bz;  // Controlled_Buffer controlled_buffer_4
  Hex_Digit_Display hex_digit_display_1 (.value(h2bcd_1_hundred));  // open: dp
  Hex_Digit_Display hex_digit_display_2 (.value(h2bcd_1_ten));  // open: dp
  h2bcd h2bcd_1 (
    .\input (MBR_q), .hundred(h2bcd_1_hundred), .ten(h2bcd_1_ten), .single(h2bcd_1_single),
    .Sign(h2bcd_1_sign));
  Subtractor #(.width(3)) subtractor_1 (.a(IR_q_2), .b(3'b010), .out(subtractor_1_out));  // open: bin, bout
  Hex_Digit_Display hex_digit_display_3 (.value(h2bcd_1_single));  // open: dp
  alu alu_1 (
    .Input_1(MBR_q), .Output(controlled_buffer_2_out), .Input_2(D0_q), .FunCode(subtractor_1_out[1:0]),
    .z(z), .C_ALU(in_11), .E_ALU(in_10));

  // Notes on the sheet:
  //   PC+1
  //   INC_PC
  //   Need 2 more 
  //   n/PC+1
  //   Version 01 -- Data Path with 'traffic lights'
  //   (1) PC automatically inc by 1
  //   (2) each instruction (from MEM) be parsed by IR
  //   ***** Build CPU = Data Path + Control
  //   C_PC
  //   E_PC
  //   (MDR)
  //   ***** Control => turn on some traffic lights PLUS trigger some DO IT signals for each instruction at each mini-step
  //   MEM
  //   C_MEM
  //   E_MEM
  //   BUS
  //   OPCODE4-6
  //   E_D0(MDR)
  //   E_IR
endmodule

// H2BCD
module h2bcd (
  input  [7:0] \input ,
  output [3:0] hundred,
  output [3:0] ten,
  output Sign,
  output [3:0] single
);

  wire [7:0] adder_1_out, divider_1_rem, multiplexer_1_out, not_1_out;
  wire [7:4] divider_1_out, divider_2_out, divider_2_rem;

  assign not_1_out = ~\input ;  // NOT_Gate not_1, 8 bits wide
  Adder adder_1 (.a(not_1_out), .b(8'h1), .out(adder_1_out));  // open: cin, cout
  BitSelector bitselector_1 (.in(\input ), .out(Sign), .sel(3'b111));
  Multiplexer #(.width(8)) multiplexer_1 (
    .in0(\input ), .in1(adder_1_out), .out(multiplexer_1_out), .sel(Sign));  // open: en
  Divider divider_1 (
    .a(multiplexer_1_out), .b(8'h64), .out({divider_1_out, hundred}), .upper({8{1'b0}}), .rem(divider_1_rem));
  Divider divider_2 (
    .a(divider_1_rem), .b(8'ha), .out({divider_2_out, ten}), .upper({8{1'b0}}), .rem({divider_2_rem, single}));
endmodule

// ALU
module alu (
  input  [7:0] Input_1,
  input  [7:0] Input_2,
  input  E_ALU,
  input  [1:0] FunCode,
  input  C_ALU,
  output [7:0] Output,
  output z
);

  wire comparator_1_eq;
  wire [3:0] bitadder_1_out;
  wire [7:0] adder_1_out, adder_2_out, multiplexer_1_out, register_1_q, register_2_q, subtractor_1_out,
       subtractor_2_out;

  Register #(.trigger("high")) register_1 (.D(Input_1), .Q(register_1_q), .clk(C_ALU));  // open: en, clr
  Register #(.trigger("high")) register_2 (.D(Input_2), .Q(register_2_q), .clk(C_ALU));  // open: en, clr
  Adder adder_1 (.a(register_1_q), .b(register_2_q), .out(adder_1_out));  // open: cin, cout
  Subtractor subtractor_1 (.a(register_2_q), .b(register_1_q), .out(subtractor_1_out));  // open: bin, bout
  Adder adder_2 (.a(register_1_q), .b(8'h1), .out(adder_2_out));  // open: cin, cout
  Subtractor subtractor_2 (.a(register_1_q), .b(8'h1), .out(subtractor_2_out));  // open: bin, bout
  Multiplexer #(.select(2), .width(8), .disabled(0), .enable("false")) multiplexer_1 (
    .in0(adder_1_out), .in1(subtractor_1_out), .in2(adder_2_out), .in3(subtractor_2_out),
    .out(multiplexer_1_out), .sel(FunCode));
  BitAdder bitadder_1 (.in0(multiplexer_1_out), .out(bitadder_1_out));
  assign Output = E_ALU ? multiplexer_1_out : 8'bz;  // Controlled_Buffer controlled_buffer_1
  Comparator #(.width(4)) comparator_1 (.a(bitadder_1_out), .b(4'b0000), .eq(comparator_1_eq));  // open: gt, lt
  Register #(.width(1), .trigger("high")) register_3 (.D(comparator_1_eq), .Q(z), .clk(C_ALU));  // open: en, clr
endmodule

module sub (
  input  CLOCK,
  input  [2:0] OPCODE,
  output CYC2,
  output CYC1,
  output CYC0,
  output S1_7,
  output S1_6,
  output S1_2_5,
  output S1_1,
  output S1_0,
  output S0_0_5,
  output M0_6_7,
  output S3_2_3,
  output S2_2_5,
  output S3_4_5
);

  wire decoder_1_out3, decoder_1_out4, decoder_1_out5, decoder_1_out6, decoder_1_out7, decoder_2_out0,
       decoder_2_out1, decoder_2_out2, decoder_2_out3, decoder_2_out4, decoder_2_out5, decoder_2_out6,
       decoder_2_out7, decoder_3_out0, decoder_3_out1, decoder_3_out2, decoder_3_out3, decoder_3_out4,
       decoder_3_out5, decoder_3_out6, decoder_3_out7, decoder_4_out2, decoder_4_out3, decoder_4_out4,
       decoder_4_out5, decoder_5_out2, decoder_5_out3, decoder_5_out4, decoder_5_out5, or_1_out, or_4_out;
  wire [2:0] counter_1_q;

  Decoder #(.select(3), .enable("false")) decoder_1 (
    .out0(CYC0), .out1(CYC1), .out2(CYC2), .out3(decoder_1_out3), .out4(decoder_1_out4),
    .out5(decoder_1_out5), .out6(decoder_1_out6), .out7(decoder_1_out7), .sel(counter_1_q));
  Counter #(.width(3), .max('h7)) counter_1 (
    .Q(counter_1_q), .clk(CLOCK), .clr(or_1_out));  // open: load, D, count, carry
  or or_1 (or_1_out, or_4_out, decoder_1_out7);
  Decoder #(.select(3), .disabled(0)) decoder_2 (
    .out0(decoder_2_out0), .out1(decoder_2_out1), .out2(decoder_2_out2), .out3(decoder_2_out3),
    .out4(decoder_2_out4), .out5(decoder_2_out5), .out6(decoder_2_out6), .out7(decoder_2_out7), .sel(OPCODE),
    .en(decoder_1_out3));
  Decoder #(.select(3), .disabled(0)) decoder_3 (
    .out0(decoder_3_out0), .out1(decoder_3_out1), .out2(decoder_3_out2), .out3(decoder_3_out3),
    .out4(decoder_3_out4), .out5(decoder_3_out5), .out6(decoder_3_out6), .out7(decoder_3_out7), .sel(OPCODE),
    .en(decoder_1_out5));
  or or_2 (S0_0_5, decoder_2_out0, decoder_2_out1, decoder_2_out2, decoder_2_out3, decoder_2_out4, decoder_2_out5);
  or or_3 (M0_6_7, decoder_2_out6, decoder_2_out7);
  or or_4 (or_4_out, decoder_3_out0, decoder_3_out1, decoder_3_out6, decoder_3_out7);
  or or_5 (S2_2_5, decoder_3_out2, decoder_3_out3, decoder_3_out4, decoder_3_out5);
  Decoder #(.select(3), .disabled(0)) decoder_4 (
    .out0(S1_0), .out1(S1_1), .out2(decoder_4_out2), .out3(decoder_4_out3), .out4(decoder_4_out4),
    .out5(decoder_4_out5), .out6(S1_6), .out7(S1_7), .sel(OPCODE), .en(decoder_1_out4));
  Decoder #(.select(3), .disabled(0)) decoder_5 (
    .out2(decoder_5_out2), .out3(decoder_5_out3), .out4(decoder_5_out4), .out5(decoder_5_out5), .sel(OPCODE),
    .en(decoder_1_out6));  // open: out0, out1, out6, out7
  or or_6 (S3_2_3, decoder_5_out2, decoder_5_out3);
  or or_7 (S3_4_5, decoder_5_out4, decoder_5_out5);
  or or_8 (S1_2_5, decoder_4_out2, decoder_4_out3, decoder_4_out4, decoder_4_out5);

  // Notes on the sheet:
  //   C_RESET
  //   SUB_0
  //   SUB_2
  //   MAR <-IR0-3
  //   PC <- IR0-3
  //   ALU <- MBR, D0
  //   SUB_1
  //   SUB_3
  //   D0 <-[MAR]
  //   MDR<-ALU
  //   MDR <- D0
  //   MBR <-[MAR]
  //   PC <-IRO-3
  //   D0<-ALU
endmodule

module control (
  input  z,
  input  CLOCK,
  input  [2:0] OPCODE,
  output INC_PC,
  output C_PC,
  output E_MEM,
  output C_IR,
  output C_MBR,
  output E_PC,
  output out_10,
  output out_11,
  output C_D0,
  output C_MEM,
  output E_ALU,
  output E_IR,
  output C_ALU
);

  wire and_1_out, sub_1_cyc2, sub_1_m0_6_7, sub_1_s0_0_5, sub_1_s1_0, sub_1_s1_6, sub_1_s1_7, sub_1_s3_2_3,
       sub_1_s3_4_5;

  or or_1 (C_IR, sub_1_cyc2, E_PC);
  or or_2 (INC_PC, out_11, sub_1_s0_0_5);
  or or_3 (C_PC, sub_1_cyc2, sub_1_s1_6, and_1_out);
  or or_4 (E_MEM, E_PC, out_10, sub_1_s1_0);
  sub sub_1 (
    .CLOCK(CLOCK), .S0_0_5(sub_1_s0_0_5), .M0_6_7(sub_1_m0_6_7), .OPCODE(OPCODE), .S3_2_3(sub_1_s3_2_3),
    .S2_2_5(C_ALU), .S3_4_5(sub_1_s3_4_5), .CYC0(out_11), .CYC1(E_PC), .CYC2(sub_1_cyc2), .S1_0(sub_1_s1_0),
    .S1_1(C_MBR), .S1_2_5(out_10), .S1_6(sub_1_s1_6), .S1_7(sub_1_s1_7));
  and and_1 (and_1_out, z, sub_1_s1_7);
  or or_5 (C_D0, sub_1_s1_0, sub_1_s3_2_3);
  or or_6 (C_MEM, C_MBR, sub_1_s3_4_5);
  or or_7 (E_ALU, sub_1_s3_4_5, sub_1_s3_2_3, C_ALU);
  or or_8 (E_IR, sub_1_s0_0_5, sub_1_s1_6, sub_1_s1_7, sub_1_m0_6_7);

  // Notes on the sheet:
  //   C_MAR
  //   E_D0(MDR)
endmodule

module CPU (
);

  wire C_ALU, C_D0, C_IR, C_MAR, C_MBR, C_MEM, C_PC, CLOCK_out, E_ALU, E_D0_MDR, E_IR, E_MEM, E_PC,
       h2bcd_1_sign, INC_PC, Z;
  wire [2:0] OPCODE, subtractor_1_out;
  wire [3:0] adder_1_out, controlled_buffer_1_out, h2bcd_1_hundred, h2bcd_1_single, h2bcd_1_ten, MAR_q,
       multiplexer_1_out, PC_q;
  wire [7:0] controlled_buffer_2_out, D0_q, IR_q, MBR_q, ram_1_data;

  Clock CLOCK (.out(CLOCK_out));
  Adder #(.width(4)) adder_1 (.a(PC_q), .b(4'b0001), .out(adder_1_out));  // open: cin, cout
  Multiplexer #(.width(4), .enable("false")) multiplexer_1 (
    .in0(controlled_buffer_1_out), .in1(adder_1_out), .out(multiplexer_1_out), .sel(INC_PC));
  Register #(.width(4)) PC (.D(multiplexer_1_out), .Q(PC_q), .clk(C_PC));  // open: en, clr
  assign controlled_buffer_1_out = E_PC ? PC_q : 4'bz;  // Controlled_Buffer controlled_buffer_1
  control control_1 (
    .CLOCK(CLOCK_out), .z(Z), .C_D0(C_D0), .C_MEM(C_MEM), .E_ALU(E_ALU), .OPCODE(OPCODE), .E_IR(E_IR),
    .C_ALU(C_ALU), .out_11(E_PC), .E_PC(C_IR), .C_IR(INC_PC), .INC_PC(C_MAR), .C_PC(C_PC), .E_MEM(E_MEM),
    .C_MBR(E_D0_MDR), .out_10(C_MBR));
  Register #(.width(4), .trigger("high")) MAR (.D(controlled_buffer_1_out), .Q(MAR_q), .clk(C_MAR));  // open: en, clr
  RAM #(.addrWidth(4), .bus("separate")) ram_1 (
    .addr(MAR_q), .din(controlled_buffer_2_out), .data(ram_1_data), .clk(C_MEM));  // open: str, sel, ld, clr
  assign controlled_buffer_2_out = E_MEM ? ram_1_data : 8'bz;  // Controlled_Buffer controlled_buffer_2
  Register #(.trigger("high")) MBR (.D(controlled_buffer_2_out), .Q(MBR_q), .clk(C_MBR));  // open: en, clr
  Register #(.trigger("high")) D0 (.D(controlled_buffer_2_out), .Q(D0_q), .clk(C_D0));  // open: en, clr
  Register #(.trigger("high")) IR (
    .D(controlled_buffer_2_out), .Q({IR_q[7], OPCODE, IR_q[3:0]}), .clk(C_IR));  // open: en, clr
  _7_Segment_Display u_7_segment_display_1 (.g(h2bcd_1_sign));  // open: f, a, b, e, d, c, dp
  assign controlled_buffer_2_out = E_D0_MDR ? D0_q : 8'bz;  // Controlled_Buffer controlled_buffer_3
  assign controlled_buffer_1_out = E_IR ? IR_q[3:0] : 4'bz;  // Controlled_Buffer controlled_buffer_4
  Hex_Digit_Display hex_digit_display_1 (.value(h2bcd_1_hundred));  // open: dp
  Hex_Digit_Display hex_digit_display_2 (.value(h2bcd_1_ten));  // open: dp
  h2bcd h2bcd_1 (
    .\input (MBR_q), .hundred(h2bcd_1_hundred), .ten(h2bcd_1_ten), .single(h2bcd_1_single),
    .Sign(h2bcd_1_sign));
  Subtractor #(.width(3)) subtractor_1 (.a(OPCODE), .b(3'b010), .out(subtractor_1_out));  // open: bin, bout
  Hex_Digit_Display hex_digit_display_3 (.value(h2bcd_1_single));  // open: dp
  alu alu_1 (
    .Input_1(MBR_q), .Output(controlled_buffer_2_out), .Input_2(D0_q), .FunCode(subtractor_1_out[1:0]),
    .z(Z), .C_ALU(C_ALU), .E_ALU(E_ALU));

  // Notes on the sheet:
  //   PC+1
  //   INC_PC
  //   n/PC+1
  //   C_PC
  //   E_PC
  //   C_MAR
  //   (MDR)
  //   MEM
  //   C_MEM
  //   E_MEM
  //   C_MBR
  //   BUS
  //   C_D0
  //   OPCODE4-6
  //   C_IR
  //   OPERAND0-3
  //   E_D0(MDR)
  //   E_IR
endmodule

module microcode (
  input  z,
  input  [2:0] OPCODE,
  input  CLOCK,
  output E_PC,
  output C_MAR,
  output C_IR,
  output E_MEM,
  output INC_PC,
  output C_PC,
  output E_IR,
  output C_MBR,
  output C_D0,
  output E_D0,
  output C_MEM,
  output C_ALU,
  output E_ALU
);

  wire and_1_out;
  wire [2:0] counter_1_q;
  wire [15:5] rom_1_data;

  Counter #(.width(3), .max('h7)) counter_1 (
    .Q(counter_1_q), .clk(CLOCK), .clr(rom_1_data[14]));  // open: load, D, count, carry
  ROM #(.addrWidth(6), .dataWidth(16)) rom_1 (
    .addr({counter_1_q, OPCODE}),
    .data({rom_1_data[15:14], E_ALU, C_ALU, rom_1_data[11], E_D0, C_D0, C_MBR, E_IR, rom_1_data[6:5], INC_PC, E_MEM, C_IR, C_MAR, E_PC}));  // open: sel
  and and_1 (and_1_out, rom_1_data[6], z);
  or or_1 (C_PC, rom_1_data[5], and_1_out);
  buf buffer_1 (C_MEM, rom_1_data[11]);

  // Notes on the sheet:
  //   contents of rom_1 (hex, n*v repeats v):
  //   8*3 8*1c 8*30 6*82 80 80 208 c00 4*108 a0 c0 4000 4000 4*3000 4*4000 2200 2200 2800 2800 10*4000
  //   CLK_RESET
endmodule

module CPU2 (
);

  wire C_ALU, C_D0, C_IR, C_MAR, C_MBR, C_MEM, C_PC, CLOCK_out, E_ALU, E_D0_MDR, E_IR, E_MEM, E_PC,
       h2bcd_1_sign, INC_PC, Z;
  wire [2:0] OPCODE, subtractor_1_out;
  wire [3:0] adder_1_out, controlled_buffer_1_out, h2bcd_1_hundred, h2bcd_1_single, h2bcd_1_ten, MAR_q,
       multiplexer_1_out, PC_q;
  wire [7:0] controlled_buffer_2_out, D0_q, IR_q, MBR_q, ram_1_data;

  Clock CLOCK (.out(CLOCK_out));
  Adder #(.width(4)) adder_1 (.a(PC_q), .b(4'b0001), .out(adder_1_out));  // open: cin, cout
  Multiplexer #(.width(4), .enable("false")) multiplexer_1 (
    .in0(controlled_buffer_1_out), .in1(adder_1_out), .out(multiplexer_1_out), .sel(INC_PC));
  Register #(.width(4)) PC (.D(multiplexer_1_out), .Q(PC_q), .clk(C_PC));  // open: en, clr
  assign controlled_buffer_1_out = E_PC ? PC_q : 4'bz;  // Controlled_Buffer controlled_buffer_1
  microcode microcode_1 (
    .z(Z), .E_PC(E_PC), .C_MAR(C_MAR), .C_IR(C_IR), .E_MEM(E_MEM), .INC_PC(INC_PC), .C_PC(C_PC), .E_IR(E_IR),
    .C_MBR(C_MBR), .C_D0(C_D0), .E_D0(E_D0_MDR), .C_MEM(C_MEM), .C_ALU(C_ALU), .E_ALU(E_ALU),
    .CLOCK(CLOCK_out), .OPCODE(OPCODE));
  Register #(.width(4), .trigger("high")) MAR (.D(controlled_buffer_1_out), .Q(MAR_q), .clk(C_MAR));  // open: en, clr
  assign controlled_buffer_2_out = E_MEM ? ram_1_data : 8'bz;  // Controlled_Buffer controlled_buffer_2
  RAM #(.addrWidth(4), .bus("separate")) ram_1 (
    .addr(MAR_q), .din(controlled_buffer_2_out), .data(ram_1_data), .clk(C_MEM));  // open: str, sel, ld, clr
  Register #(.trigger("high")) MBR (.D(controlled_buffer_2_out), .Q(MBR_q), .clk(C_MBR));  // open: en, clr
  Register #(.trigger("high")) D0 (.D(controlled_buffer_2_out), .Q(D0_q), .clk(C_D0));  // open: en, clr
  Register #(.trigger("high")) IR (
    .D(controlled_buffer_2_out), .Q({IR_q[7], OPCODE, IR_q[3:0]}), .clk(C_IR));  // open: en, clr
  _7_Segment_Display u_7_segment_display_1 (.g(h2bcd_1_sign));  // open: f, a, b, e, d, c, dp
  assign controlled_buffer_2_out = E_D0_MDR ? D0_q : 8'bz;  // Controlled_Buffer controlled_buffer_3
  assign controlled_buffer_1_out = E_IR ? IR_q[3:0] : 4'bz;  // Controlled_Buffer controlled_buffer_4
  Hex_Digit_Display hex_digit_display_1 (.value(h2bcd_1_ten));  // open: dp
  Hex_Digit_Display hex_digit_display_2 (.value(h2bcd_1_hundred));  // open: dp
  h2bcd h2bcd_1 (
    .\input (MBR_q), .hundred(h2bcd_1_hundred), .ten(h2bcd_1_ten), .single(h2bcd_1_single),
    .Sign(h2bcd_1_sign));
  Subtractor #(.width(3)) subtractor_1 (.a(OPCODE), .b(3'b010), .out(subtractor_1_out));  // open: bin, bout
  Hex_Digit_Display hex_digit_display_3 (.value(h2bcd_1_single));  // open: dp
  alu alu_1 (
    .Input_1(MBR_q), .Output(controlled_buffer_2_out), .Input_2(D0_q), .FunCode(subtractor_1_out[1:0]),
    .z(Z), .C_ALU(C_ALU), .E_ALU(E_ALU));

  // Notes on the sheet:
  //   PC+1
  //   INC_PC
  //   n/PC+1
  //   C_PC
  //   E_PC
  //   C_MAR
  //   (MDR)
  //   MEM
  //   C_MEM
  //   E_MEM
  //   C_MBR
  //   BUS
  //   C_D0
  //   OPCODE4-6
  //   C_IR
  //   OPERAND0-3
  //   E_D0(MDR)
  //   E_IR
endmodule
