// Logisim project homework3.circ as structural Verilog: 6 circuits, main circuit main
module main (
  input  in_1,
  input  in_2,
  input  C_MAR,
  input  in_4,
  input  in_5,
  input  in_6,
  input  C_MBR,
  input  C_D0,
  input  in_9,
  input  in_10,
  input  in_11,
  input  C_IR,
  input  OPERAND0_3,
  output z
);

  wire h2bcd_1_sign;
  wire [2:0] IR_q_2, subtractor_1_out;
  wire [3:0] adder_1_out, controlled_buffer_1_out, h2bcd_1_hundred, h2bcd_1_single, h2bcd_1_ten, MAR_q,
       multiplexer_1_out, PC_q;
  wire [7:0] controlled_buffer_2_out, D0_q, IR_q, MBR_q, ram_1_data;

  Adder #(.width(4)) adder_1 (.a(PC_q), .b(4'b0001), .out(adder_1_out));  // open: cin, cout
  Multiplexer #(.width(4), .enable("false")) multiplexer_1 (
    .in0(controlled_buffer_1_out), .in1(adder_1_out), .out(multiplexer_1_out), .sel(in_1));
  Register #(.width(4)) PC (.D(multiplexer_1_out), .Q(PC_q), .clk(in_2));  // open: en, clr
  assign controlled_buffer_1_out = C_MAR ? PC_q : 4'bz;  // Controlled_Buffer controlled_buffer_1
  Register #(.width(4), .trigger("high")) MAR (.D(controlled_buffer_1_out), .Q(MAR_q), .clk(in_4));  // open: en, clr
  RAM #(.addrWidth(4), .bus("separate")) ram_1 (
    .addr(MAR_q), .din(controlled_buffer_2_out), .data(ram_1_data), .clk(in_5));  // open: str, sel, ld, clr
  assign controlled_buffer_2_out = in_6 ? ram_1_data : 8'bz;  // Controlled_Buffer controlled_buffer_2
  Register #(.trigger("high")) MBR (.D(controlled_buffer_2_out), .Q(MBR_q), .clk(C_MBR));  // open: en, clr
  Register #(.trigger("high")) D0 (.D(controlled_buffer_2_out), .Q(D0_q), .clk(C_D0));  // open: en, clr
  Register #(.trigger("high")) IR (
    .D(controlled_buffer_2_out), .Q({IR_q[7], IR_q_2, IR_q[3:0]}), .clk(C_IR));  // open: en, clr
  _7_Segment_Display u_7_segment_display_1 (.g(h2bcd_1_sign));  // open: f, a, b, e, d, c, dp
  assign controlled_buffer_2_out = in_9 ? D0_q : 8'bz;  // Controlled_Buffer controlled_buffer_3
  assign controlled_buffer_1_out = OPERAND0_3 ? IR_q[3:0] : 4'bz;  // Controlled_Buffer controlled_buffer_4
  Hex_Digit_Display hex_digit_display_1 (.value(h2bcd_1_hundred));  // open: dp
  Hex_Digit_Display hex_digit_display_2 (.value(h2bcd_1_ten));  // open: dp
  h2bcd h2bcd_1 (
    .\input (MBR_q), .hundred(h2bcd_1_hundred), .ten(h2bcd_1_ten), .single(h2bcd_1_single),
    .Sign(h2bcd_1_sign));
  Subtractor #(.width(3)) subtractor_1 (.a(IR_q_2), .b(3'b010), .out(subtractor_1_out));  // open: bin, bout
  Hex_Digit_Display hex_digit_display_3 (.value(h2bcd_1_single));  // open: dp
  alu alu_1 (
    .Input_1(MBR_q), .Input_2(D0_q), .Output(controlled_buffer_2_out), .E_ALU(in_10), .z(z),
    .FunCode(subtractor_1_out[1:0]), .C_ALU(in_11));

  // Notes on the sheet:
  //   PC+1
  //   INC_PC
  //   n/PC+1
  //   C_PC
  //   E_PC
  //   (MDR)
  //   MEM
  //   C_MEM
  //   E_MEM
  //   BUS
  //   OPCODE4-6
  //   E_D0(MDR)
  //   E_IR
endmodule

// H2BCD
module h2bcd (
  input  [7:0] \input ,
  output [3:0] hundred,
  output [3:0] ten,
  output Sign,
  output [3:0] single
);

  wire [7:0] adder_1_out, divider_1_rem, multiplexer_1_out, not_1_out;
  wire [7:4] divider_1_out, divider_2_out, divider_2_rem;

  assign not_1_out = ~\input ;  // NOT_Gate not_1, 8 bits wide
  Adder adder_1 (.a(not_1_out), .b(8'h1), .out(adder_1_out));  // open: cin, cout
  BitSelector bitselector_1 (.in(\input ), .out(Sign), .sel(3'b111));
  Multiplexer #(.width(8)) multiplexer_1 (
    .in0(\input ), .in1(adder_1_out), .out(multiplexer_1_out), .sel(Sign));  // open: en
  Divider divider_1 (
    .a(multiplexer_1_out), .b(8'h64), .out({divider_1_out, hundred}), .upper({8{1'b0}}), .rem(divider_1_rem));
  Divider divider_2 (
    .a(divider_1_rem), .b(8'ha), .out({divider_2_out, ten}), .upper({8{1'b0}}), .rem({divider_2_rem, single}));
endmodule

// ALU
module alu (
  input  [7:0] Input_1,
  input  [7:0] Input_2,
  input  E_ALU,
  input  [1:0] FunCode,
  input  C_ALU,
  output [7:0] Output,
  output z
);

  wire comparator_1_eq;
  wire [3:0] bitadder_1_out;
  wire [7:0] adder_1_out, and_1_out, multiplexer_1_out, register_1_q, register_2_q, shifter_1_out;

  Register #(.trigger("high")) register_1 (.D(Input_1), .Q(register_1_q), .clk(C_ALU));  // open: en, clr
  Register #(.trigger("high")) register_2 (.D(Input_2), .Q(register_2_q), .clk(C_ALU));  // open: en, clr
  Adder adder_1 (.a(register_1_q), .b(register_2_q), .out(adder_1_out));  // open: cin, cout
  assign and_1_out = register_1_q & register_2_q;  // AND_Gate and_1, 8 bits wide
  Shifter shifter_1 (.in(register_1_q), .\dist (3'b001), .out(shifter_1_out));
  Multiplexer #(.select(2), .width(8), .enable("false")) multiplexer_1 (
    .in0(adder_1_out), .in1(and_1_out), .in2(shifter_1_out), .in3({8{1'b0}}), .out(multiplexer_1_out),
    .sel(FunCode));
  BitAdder bitadder_1 (.in0(multiplexer_1_out), .out(bitadder_1_out));
  assign Output = E_ALU ? multiplexer_1_out : 8'bz;  // Controlled_Buffer controlled_buffer_1
  Comparator #(.width(4)) comparator_1 (.a(bitadder_1_out), .b(4'b0000), .eq(comparator_1_eq));  // open: gt, lt
  Register #(.width(1), .trigger("high")) register_3 (.D(comparator_1_eq), .Q(z), .clk(C_ALU));  // open: en, clr

  // Notes on the sheet:
  //   0 ADD
  //   1 AND
  //   2 SHL
endmodule

module sub (
  input  [2:0] OPCODE,
  input  CLK,
  input  C_RESET,
  output S0_7,
  output S1_7,
  output S2_7,
  output S3_7,
  output S0_6,
  output S1_6,
  output S2_6,
  output S3_6,
  output S0_5,
  output S1_5,
  output S2_5,
  output S3_5,
  output S0_4,
  output S1_4,
  output S2_4,
  output S3_4,
  output S0_3,
  output S1_3,
  output S2_3,
  output S3_3,
  output S0_2,
  output S1_2,
  output S2_2,
  output S3_2,
  output S0_1,
  output S1_1,
  output S2_1,
  output S3_1,
  output S0_0,
  output S1_0,
  output S2_0,
  output S3_0,
  output S4_7,
  output S5_7,
  output S6_7,
  output S7_7,
  output S4_6,
  output S5_6,
  output S6_6,
  output S7_6,
  output S4_5,
  output S5_5,
  output S6_5,
  output S7_5,
  output S4_4,
  output S5_4,
  output S6_4,
  output S7_4,
  output S4_3,
  output S5_3,
  output S6_3,
  output S7_3,
  output S4_2,
  output S5_2,
  output S6_2,
  output S7_2,
  output S4_1,
  output S5_1,
  output S6_1,
  output S7_1,
  output S4_0,
  output S5_0,
  output S6_0,
  output S7_0
);

  wire decoder_1_out0, decoder_1_out1, decoder_1_out2, decoder_1_out3, decoder_1_out4, decoder_1_out5,
       decoder_1_out6, decoder_1_out7;
  wire [2:0] counter_1_q;

  Counter #(.width(3), .max('h7)) counter_1 (.Q(counter_1_q), .clk(CLK), .clr(C_RESET));  // open: load, D, count, carry
  Decoder #(.select(3), .enable("false")) decoder_1 (
    .out0(decoder_1_out0), .out1(decoder_1_out1), .out2(decoder_1_out2), .out3(decoder_1_out3),
    .out4(decoder_1_out4), .out5(decoder_1_out5), .out6(decoder_1_out6), .out7(decoder_1_out7),
    .sel(counter_1_q));
  Decoder #(.select(3), .disabled(0)) decoder_2 (
    .out0(S0_0), .out1(S0_1), .out2(S0_2), .out3(S0_3), .out4(S0_4), .out5(S0_5), .out6(S0_6), .out7(S0_7),
    .sel(OPCODE), .en(decoder_1_out0));
  Decoder #(.select(3), .disabled(0)) decoder_3 (
    .out0(S4_0), .out1(S4_1), .out2(S4_2), .out3(S4_3), .out4(S4_4), .out5(S4_5), .out6(S4_6), .out7(S4_7),
    .sel(OPCODE), .en(decoder_1_out4));
  Decoder #(.select(3), .disabled(0)) decoder_4 (
    .out0(S1_0), .out1(S1_1), .out2(S1_2), .out3(S1_3), .out4(S1_4), .out5(S1_5), .out6(S1_6), .out7(S1_7),
    .sel(OPCODE), .en(decoder_1_out1));
  Decoder #(.select(3), .disabled(0)) decoder_5 (
    .out0(S5_0), .out1(S5_1), .out2(S5_2), .out3(S5_3), .out4(S5_4), .out5(S5_5), .out6(S5_6), .out7(S5_7),
    .sel(OPCODE), .en(decoder_1_out5));
  Decoder #(.select(3), .disabled(0)) decoder_6 (
    .out0(S2_0), .out1(S2_1), .out2(S2_2), .out3(S2_3), .out4(S2_4), .out5(S2_5), .out6(S2_6), .out7(S2_7),
    .sel(OPCODE), .en(decoder_1_out2));
  Decoder #(.select(3), .disabled(0)) decoder_7 (
    .out0(S6_0), .out1(S6_1), .out2(S6_2), .out3(S6_3), .out4(S6_4), .out5(S6_5), .out6(S6_6), .out7(S6_7),
    .sel(OPCODE), .en(decoder_1_out6));
  Decoder #(.select(3), .disabled(0)) decoder_8 (
    .out0(S3_0), .out1(S3_1), .out2(S3_2), .out3(S3_3), .out4(S3_4), .out5(S3_5), .out6(S3_6), .out7(S3_7),
    .sel(OPCODE), .en(decoder_1_out3));
  Decoder #(.select(3), .disabled(0)) decoder_9 (
    .out0(S7_0), .out1(S7_1), .out2(S7_2), .out3(S7_3), .out4(S7_4), .out5(S7_5), .out6(S7_6), .out7(S7_7),
    .sel(OPCODE), .en(decoder_1_out7));

  // Notes on the sheet:
  //   SUB_0
  //   SUB_4
  //   SUB_1
  //   SUB_5
  //   SUB_2
  //   SUB_6
  //   SUB_3
  //   SUB_7
endmodule

module Control (
  input  z,
  input  CLOCK,
  input  [2:0] OPCODE,
  output E_PC,
  output C_MAR,
  output C_IR,
  output E_MEM,
  output INC_PC,
  output C_PC,
  output E_IR,
  output C_MBR,
  output C_D0,
  output E_D0,
  output C_MEM,
  output C_ALU,
  output E_ALU
);

  wire and_1_out, or_3_out, or_4_out, or_5_out, or_7_out, or_9_out, or_10_out, or_11_out, or_12_out,
       or_13_out, or_22_out, sub_1_s0_0, sub_1_s0_1, sub_1_s0_2, sub_1_s0_3, sub_1_s0_4, sub_1_s0_5,
       sub_1_s0_6, sub_1_s0_7, sub_1_s1_0, sub_1_s1_1, sub_1_s1_2, sub_1_s1_3, sub_1_s1_4, sub_1_s1_5,
       sub_1_s1_6, sub_1_s1_7, sub_1_s2_0, sub_1_s2_1, sub_1_s2_2, sub_1_s2_3, sub_1_s2_4, sub_1_s2_5,
       sub_1_s2_6, sub_1_s2_7, sub_1_s3_0, sub_1_s3_1, sub_1_s3_2, sub_1_s3_3, sub_1_s3_4, sub_1_s3_5,
       sub_1_s3_6, sub_1_s3_7, sub_1_s4_0, sub_1_s4_2, sub_1_s4_3, sub_1_s4_4, sub_1_s4_5, sub_1_s4_6,
       sub_1_s4_7, sub_1_s5_0, sub_1_s5_1, sub_1_s5_2, sub_1_s5_3, sub_1_s5_4, sub_1_s5_5, sub_1_s5_6,
       sub_1_s5_7, sub_1_s6_0, sub_1_s6_1, sub_1_s6_2, sub_1_s6_3, sub_1_s6_4, sub_1_s6_5, sub_1_s6_6,
       sub_1_s6_7, sub_1_s7_0, sub_1_s7_1, sub_1_s7_2, sub_1_s7_3, sub_1_s7_4, sub_1_s7_5, sub_1_s7_6,
       sub_1_s7_7;

  or or_1 (E_PC, sub_1_s0_0, sub_1_s0_1, sub_1_s0_2, sub_1_s0_3, sub_1_s0_4, sub_1_s0_5, sub_1_s0_6, sub_1_s0_7);
  or or_2 (C_IR, sub_1_s1_0, sub_1_s1_1, sub_1_s1_2, sub_1_s1_3, sub_1_s1_4, sub_1_s1_5, sub_1_s1_6, sub_1_s1_7);
  or or_3 (or_3_out, sub_1_s2_0, sub_1_s2_1, sub_1_s2_2, sub_1_s2_3, sub_1_s2_4, sub_1_s2_5, sub_1_s2_6, sub_1_s2_7);
  or or_4 (or_4_out, sub_1_s3_6, sub_1_s3_7);
  or or_5 (or_5_out, sub_1_s3_0, sub_1_s3_1, sub_1_s3_2, sub_1_s3_3, sub_1_s3_4, sub_1_s3_5);
  or or_6 (C_MBR, sub_1_s4_2, sub_1_s4_3, sub_1_s4_4, sub_1_s4_5);
  or or_7 (or_7_out, sub_1_s5_0, sub_1_s5_1);
  or or_8 (C_ALU, sub_1_s5_2, sub_1_s5_3, sub_1_s5_4, sub_1_s5_5);
  or or_9 (or_9_out, sub_1_s5_6, sub_1_s5_7, sub_1_s6_0, sub_1_s6_1);
  or or_10 (or_10_out, sub_1_s6_2, sub_1_s6_3);
  or or_11 (or_11_out, sub_1_s6_4, sub_1_s6_5);
  or or_12 (or_12_out, sub_1_s6_6, sub_1_s6_7);
  and and_1 (and_1_out, sub_1_s4_7, z);
  or or_13 (or_13_out, sub_1_s7_0, sub_1_s7_1, sub_1_s7_2, sub_1_s7_3, sub_1_s7_4, sub_1_s7_5, sub_1_s7_6, sub_1_s7_7);
  sub sub_1 (
    .OPCODE(OPCODE), .S0_0(sub_1_s0_0), .S4_0(sub_1_s4_0), .S0_1(sub_1_s0_1), .S4_1(E_D0), .S0_2(sub_1_s0_2),
    .S4_2(sub_1_s4_2), .S0_3(sub_1_s0_3), .S4_3(sub_1_s4_3), .S0_4(sub_1_s0_4), .S4_4(sub_1_s4_4),
    .S0_5(sub_1_s0_5), .S4_5(sub_1_s4_5), .S0_6(sub_1_s0_6), .S4_6(sub_1_s4_6), .S0_7(sub_1_s0_7),
    .S4_7(sub_1_s4_7), .S1_0(sub_1_s1_0), .S5_0(sub_1_s5_0), .S1_1(sub_1_s1_1), .S5_1(sub_1_s5_1),
    .S1_2(sub_1_s1_2), .S5_2(sub_1_s5_2), .S1_3(sub_1_s1_3), .S5_3(sub_1_s5_3), .S1_4(sub_1_s1_4),
    .S5_4(sub_1_s5_4), .S1_5(sub_1_s1_5), .S5_5(sub_1_s5_5), .S1_6(sub_1_s1_6), .S5_6(sub_1_s5_6),
    .S1_7(sub_1_s1_7), .S5_7(sub_1_s5_7), .S2_0(sub_1_s2_0), .S6_0(sub_1_s6_0), .S2_1(sub_1_s2_1),
    .S6_1(sub_1_s6_1), .S2_2(sub_1_s2_2), .S6_2(sub_1_s6_2), .S2_3(sub_1_s2_3), .S6_3(sub_1_s6_3),
    .S2_4(sub_1_s2_4), .S6_4(sub_1_s6_4), .S2_5(sub_1_s2_5), .S6_5(sub_1_s6_5), .S2_6(sub_1_s2_6),
    .S6_6(sub_1_s6_6), .S2_7(sub_1_s2_7), .S6_7(sub_1_s6_7), .S3_0(sub_1_s3_0), .S7_0(sub_1_s7_0),
    .S3_1(sub_1_s3_1), .S7_1(sub_1_s7_1), .S3_2(sub_1_s3_2), .S7_2(sub_1_s7_2), .S3_3(sub_1_s3_3),
    .S7_3(sub_1_s7_3), .S3_4(sub_1_s3_4), .S7_4(sub_1_s7_4), .S3_5(sub_1_s3_5), .S7_5(sub_1_s7_5),
    .S3_6(sub_1_s3_6), .S7_6(sub_1_s7_6), .S3_7(sub_1_s3_7), .S7_7(sub_1_s7_7), .CLK(CLOCK),
    .C_RESET(or_22_out));
  or or_14 (C_MAR, E_PC, or_5_out);
  or or_15 (E_MEM, C_IR, sub_1_s4_0, C_MBR);
  or or_16 (INC_PC, C_IR, or_3_out);
  or or_17 (C_PC, or_3_out, sub_1_s4_6, and_1_out);
  or or_18 (E_IR, or_5_out, or_4_out, sub_1_s4_7, sub_1_s4_6);
  or or_19 (C_D0, sub_1_s4_0, or_10_out);
  or or_20 (C_MEM, E_D0, or_11_out);
  or or_21 (E_ALU, C_ALU, or_10_out, or_11_out);
  or or_22 (or_22_out, or_7_out, or_9_out, or_12_out, or_13_out);

  // Notes on the sheet:
  //   CLK_RESET
endmodule

module cpu (
);

  wire C_ALU, C_D0, C_IR, C_MAR, C_MBR, C_MEM, C_PC, clock_1_out, E_ALU, E_D0, E_IR, E_MEM, E_PC,
       h2bcd_1_sign, INC_PC, z;
  wire [2:0] OPCODE, subtractor_1_out;
  wire [3:0] adder_1_out, controlled_buffer_1_out, h2bcd_1_hundred, h2bcd_1_single, h2bcd_1_ten, MAR_q,
       multiplexer_1_out, PC_q;
  wire [7:0] controlled_buffer_2_out, D0_q, IR_q, MBR_q, ram_1_data;

  Adder #(.width(4)) adder_1 (.a(PC_q), .b(4'b0001), .out(adder_1_out));  // open: cin, cout
  Clock clock_1 (.out(clock_1_out));
  Multiplexer #(.width(4), .enable("false")) multiplexer_1 (
    .in0(controlled_buffer_1_out), .in1(adder_1_out), .out(multiplexer_1_out), .sel(INC_PC));
  Register #(.width(4)) PC (.D(multiplexer_1_out), .Q(PC_q), .clk(C_PC));  // open: en, clr
  assign controlled_buffer_1_out = E_PC ? PC_q : 4'bz;  // Controlled_Buffer controlled_buffer_1
  Register #(.width(4), .trigger("high")) MAR (.D(controlled_buffer_1_out), .Q(MAR_q), .clk(C_MAR));  // open: en, clr
  Control control_1 (
    .z(z), .CLOCK(clock_1_out), .E_PC(E_PC), .C_MAR(C_MAR), .C_IR(C_IR), .E_MEM(E_MEM), .INC_PC(INC_PC),
    .C_PC(C_PC), .E_IR(E_IR), .C_MBR(C_MBR), .C_D0(C_D0), .E_D0(E_D0), .C_MEM(C_MEM), .C_ALU(C_ALU),
    .E_ALU(E_ALU), .OPCODE(OPCODE));
  RAM #(.addrWidth(4), .bus("separate")) ram_1 (
    .addr(MAR_q), .din(controlled_buffer_2_out), .data(ram_1_data), .clk(C_MEM));  // open: str, sel, ld, clr
  assign controlled_buffer_2_out = E_MEM ? ram_1_data : 8'bz;  // Controlled_Buffer controlled_buffer_2
  Register #(.trigger("high")) MBR (.D(controlled_buffer_2_out), .Q(MBR_q), .clk(C_MBR));  // open: en, clr
  Register #(.trigger("high")) D0 (.D(controlled_buffer_2_out), .Q(D0_q), .clk(C_D0));  // open: en, clr
  Register #(.trigger("high")) IR (
    .D(controlled_buffer_2_out), .Q({IR_q[7], OPCODE, IR_q[3:0]}), .clk(C_IR));  // open: en, clr
  _7_Segment_Display u_7_segment_display_1 (.g(h2bcd_1_sign));  // open: f, a, b, e, d, c, dp
  assign controlled_buffer_2_out = E_D0 ? D0_q : 8'bz;  // Controlled_Buffer controlled_buffer_3
  assign controlled_buffer_1_out = E_IR ? IR_q[3:0] : 4'bz;  // Controlled_Buffer controlled_buffer_4
  Hex_Digit_Display hex_digit_display_1 (.value(h2bcd_1_ten));  // open: dp
  Hex_Digit_Display hex_digit_display_2 (.value(h2bcd_1_hundred));  // open: dp
  h2bcd h2bcd_1 (
    .\input (MBR_q), .hundred(h2bcd_1_hundred), .ten(h2bcd_1_ten), .single(h2bcd_1_single),
    .Sign(h2bcd_1_sign));
  Subtractor #(.width(3)) subtractor_1 (.a(OPCODE), .b(3'b010), .out(subtractor_1_out));  // open: bin, bout
  Hex_Digit_Display hex_digit_display_3 (.value(h2bcd_1_single));  // open: dp
  alu alu_1 (
    .Input_1(MBR_q), .Input_2(D0_q), .Output(controlled_buffer_2_out), .E_ALU(E_ALU), .z(z),
    .FunCode(subtractor_1_out[1:0]), .C_ALU(C_ALU));

  // Notes on the sheet:
  //   PC+1
  //   INC_PC
  //   n/PC+1
  //   C_PC
  //   E_PC
  //   C_MAR
  //   (MDR)
  //   MEM
  //   C_MEM
  //   E_MEM
  //   C_MBR
  //   BUS
  //   C_D0
  //   OPCODE4-6
  //   OPERAND0-3
  //   C_IR
  //   E_D0(MDR)
  //   E_IR
endmodule
