// Logisim project EstefanValencia04.circ as structural Verilog: 11 circuits, main circuit main
module main (
);

  wire alu_1_z, and_1_out, CLOCK_out, decoder_1_out0, decoder_1_out1, decoder_1_out2, decoder_1_out3,
       decoder_1_out4, decoder_1_out5, decoder_1_out6, decoder_1_out7, decoder_2_out0, decoder_2_out1,
       decoder_2_out2, decoder_2_out3, decoder_2_out4, decoder_2_out5, decoder_2_out6, decoder_2_out7,
       decoder_3_out0, decoder_3_out1, decoder_3_out2, decoder_3_out3, decoder_3_out4, decoder_3_out5,
       decoder_3_out6, decoder_3_out7, decoder_4_out0, decoder_4_out1, decoder_4_out2, decoder_4_out3,
       decoder_4_out4, decoder_4_out5, decoder_4_out6, decoder_4_out7, decoder_5_out0, decoder_5_out1,
       decoder_5_out2, decoder_5_out3, h2bcd_1_sign, or_1_out, or_2_out, or_3_out, or_4_out, or_5_out,
       or_6_out, or_7_out, or_8_out, or_9_out, or_10_out, or_11_out, or_12_out, or_13_out, or_14_out,
       or_15_out;
  wire [2:0] CYCLE_q, IR_q_2;
  wire [3:0] adder_1_out, controlled_buffer_1_out, h2bcd_1_hundred, h2bcd_1_single, h2bcd_1_ten, MAR_q,
       multiplexer_1_out, PC_q;
  wire [7:0] BCD_q, controlled_buffer_2_out, D0_q, IR_q, MBR_q, ram_1_data;

  Clock CLOCK (.out(CLOCK_out));
  Adder #(.width(4)) adder_1 (.a(PC_q), .b(4'b0001), .out(adder_1_out));  // open: cin, cout
  Decoder #(.select(3), .enable("false")) decoder_1 (
    .out0(decoder_1_out0), .out1(decoder_1_out1), .out2(decoder_1_out2), .out3(decoder_1_out3),
    .out4(decoder_1_out4), .out5(decoder_1_out5), .out6(decoder_1_out6), .out7(decoder_1_out7), .sel(CYCLE_q));
  Counter #(.width(3), .max('h7)) CYCLE (.Q(CYCLE_q), .clk(CLOCK_out), .clr(or_1_out));  // open: load, D, count, carry
  or or_1 (or_1_out, or_7_out, decoder_5_out3, decoder_1_out7);
  Multiplexer #(.width(4), .enable("false")) multiplexer_1 (
    .in0(controlled_buffer_1_out), .in1(adder_1_out), .out(multiplexer_1_out), .sel(or_2_out));
  or or_2 (or_2_out, decoder_1_out1, decoder_1_out2);
  Decoder #(.select(3), .disabled(0)) decoder_2 (
    .out0(decoder_2_out0), .out1(decoder_2_out1), .out2(decoder_2_out2), .out3(decoder_2_out3),
    .out4(decoder_2_out4), .out5(decoder_2_out5), .out6(decoder_2_out6), .out7(decoder_2_out7), .sel(IR_q_2),
    .en(decoder_1_out3));
  Decoder #(.select(3), .disabled(0)) decoder_3 (
    .out0(decoder_3_out0), .out1(decoder_3_out1), .out2(decoder_3_out2), .out3(decoder_3_out3),
    .out4(decoder_3_out4), .out5(decoder_3_out5), .out6(decoder_3_out6), .out7(decoder_3_out7), .sel(IR_q_2),
    .en(decoder_1_out5));
  Register #(.width(4)) PC (.D(multiplexer_1_out), .Q(PC_q), .clk(or_3_out));  // open: en, clr
  or or_3 (or_3_out, decoder_1_out2, and_1_out, decoder_4_out6);
  or or_4 (or_4_out, decoder_2_out0, decoder_2_out1, decoder_2_out2, decoder_2_out3, decoder_2_out4, decoder_2_out5);
  or or_5 (or_5_out, decoder_2_out6, decoder_2_out7);
  or or_6 (or_6_out, decoder_3_out0, decoder_3_out1, decoder_3_out2);
  or or_7 (or_7_out, decoder_3_out4, decoder_3_out5, decoder_3_out6, decoder_3_out7);
  assign controlled_buffer_1_out = decoder_1_out0 ? PC_q : 4'bz;  // Controlled_Buffer controlled_buffer_1
  or or_8 (or_8_out, decoder_1_out0, or_4_out);
  Decoder #(.select(3), .disabled(0)) decoder_4 (
    .out0(decoder_4_out0), .out1(decoder_4_out1), .out2(decoder_4_out2), .out3(decoder_4_out3),
    .out4(decoder_4_out4), .out5(decoder_4_out5), .out6(decoder_4_out6), .out7(decoder_4_out7), .sel(IR_q_2),
    .en(decoder_1_out4));
  Decoder #(.select(3), .disabled(0)) decoder_5 (
    .out0(decoder_5_out0), .out1(decoder_5_out1), .out2(decoder_5_out2), .out3(decoder_5_out3), .sel(IR_q_2),
    .en(decoder_1_out6));  // open: out4, out5, out6, out7
  Register #(.width(4), .trigger("high")) MAR (
    .D(controlled_buffer_1_out), .Q(MAR_q), .clk(or_8_out));  // open: en, clr
  or or_9 (or_9_out, decoder_4_out0, decoder_4_out1, decoder_4_out2, decoder_4_out3);
  or or_10 (or_10_out, decoder_5_out0, decoder_5_out1);
  or or_11 (or_11_out, decoder_5_out2, decoder_4_out5);
  RAM #(.addrWidth(4), .bus("separate")) ram_1 (
    .addr(MAR_q), .din(controlled_buffer_2_out), .data(ram_1_data), .clk(or_11_out));  // open: str, sel, ld, clr
  assign controlled_buffer_2_out = or_12_out ? ram_1_data : 8'bz;  // Controlled_Buffer controlled_buffer_2
  or or_12 (or_12_out, decoder_1_out1, or_9_out, decoder_4_out4);
  Register #(.trigger("high")) MBR (.D(controlled_buffer_2_out), .Q(MBR_q), .clk(or_9_out));  // open: en, clr
  and and_1 (and_1_out, decoder_4_out7, alu_1_z);
  Register #(.trigger("high")) D0 (.D(controlled_buffer_2_out), .Q(D0_q), .clk(or_13_out));  // open: en, clr
  or or_13 (or_13_out, decoder_4_out4, or_10_out);
  Register #(.trigger("high")) IR (
    .D(controlled_buffer_2_out), .Q({IR_q[7], IR_q_2, IR_q[3:0]}), .clk(decoder_1_out1));  // open: en, clr
  or or_14 (or_14_out, decoder_4_out7, decoder_4_out6, or_4_out, or_5_out);
  _7_Segment_Display u_7_segment_display_1 (.g(h2bcd_1_sign));  // open: f, a, b, e, d, c, dp
  Register #(.trigger("high")) BCD (.D(MBR_q), .Q(BCD_q), .clk(decoder_3_out3));  // open: en, clr
  assign controlled_buffer_2_out = decoder_4_out5 ? D0_q : 8'bz;  // Controlled_Buffer controlled_buffer_3
  assign controlled_buffer_1_out = or_14_out ? IR_q[3:0] : 4'bz;  // Controlled_Buffer controlled_buffer_4
  Hex_Digit_Display hex_digit_display_1 (.value(h2bcd_1_hundred));  // open: dp
  h2bcd h2bcd_1 (
    .\input (BCD_q), .hundred(h2bcd_1_hundred), .ten(h2bcd_1_ten), .single(h2bcd_1_single),
    .Sign(h2bcd_1_sign));
  or or_15 (or_15_out, or_10_out, decoder_5_out2, or_6_out);
  Hex_Digit_Display hex_digit_display_2 (.value(h2bcd_1_ten));  // open: dp
  Hex_Digit_Display hex_digit_display_3 (.value(h2bcd_1_single));  // open: dp
  alu alu_1 (
    .Input_1(MBR_q), .Input_2(D0_q), .Output(controlled_buffer_2_out), .E_ALU(or_15_out), .z(alu_1_z),
    .FunCode(IR_q_2[1:0]), .C_ALU(or_6_out));

  // Notes on the sheet:
  //   C_RESET
  //   PC+1
  //   INC_PC
  //   n/PC+1
  //   SUB_0
  //   SUB_2
  //   C_PC
  //   MAR<-IR0-3
  //   ALU<-MBR,D0
  //   HEX<-MBR
  //   E_PC
  //   C_MAR
  //   SUB_1
  //   SUB_3
  //   (MDR)
  //   MBR<-[MAR]
  //   PC<-IR0-3
  //   R0<-ALU
  //   MDR<-ALU
  //   MEM
  //   C_MEM
  //   D0<-[MAR]
  //   MDR<-D0
  //   E_MEM
  //   C_MBR
  //   BUS
  //   C_D0
  //   C_IR
  //   E_D0(MDR)
  //   OPCODE4-6
  //   E_IR
  //   OPERAND0-3
  //   C_BCD
  //   z
endmodule

// H2BCD
module h2bcd (
  input  [7:0] \input ,
  output [3:0] hundred,
  output [3:0] ten,
  output Sign,
  output [3:0] single
);

  wire [7:0] adder_1_out, divider_1_rem, multiplexer_1_out, not_1_out;
  wire [7:4] divider_1_out, divider_2_out, divider_2_rem;

  assign not_1_out = ~\input ;  // NOT_Gate not_1, 8 bits wide
  Adder adder_1 (.a(not_1_out), .b(8'h1), .out(adder_1_out));  // open: cin, cout
  BitSelector bitselector_1 (.in(\input ), .out(Sign), .sel(3'b111));
  Multiplexer #(.width(8)) multiplexer_1 (
    .in0(\input ), .in1(adder_1_out), .out(multiplexer_1_out), .sel(Sign));  // open: en
  Divider divider_1 (
    .a(multiplexer_1_out), .b(8'h64), .out({divider_1_out, hundred}), .upper({8{1'b0}}), .rem(divider_1_rem));
  Divider divider_2 (
    .a(divider_1_rem), .b(8'ha), .out({divider_2_out, ten}), .upper({8{1'b0}}), .rem({divider_2_rem, single}));
endmodule

// ALU
module alu (
  input  [7:0] Input_1,
  input  [7:0] Input_2,
  input  E_ALU,
  input  [1:0] FunCode,
  input  C_ALU,
  output [7:0] Output,
  output z
);

  wire comparator_1_eq;
  wire [3:0] bitadder_1_out;
  wire [7:0] adder_1_out, and_1_out, multiplexer_1_out, register_1_q, register_2_q, shifter_1_out;

  Register #(.trigger("high")) register_1 (.D(Input_1), .Q(register_1_q), .clk(C_ALU));  // open: en, clr
  Register #(.trigger("high")) register_2 (.D(Input_2), .Q(register_2_q), .clk(C_ALU));  // open: en, clr
  Adder adder_1 (.a(register_1_q), .b(register_2_q), .out(adder_1_out));  // open: cin, cout
  assign and_1_out = register_1_q & register_2_q;  // AND_Gate and_1, 8 bits wide
  Shifter shifter_1 (.in(register_1_q), .\dist (3'b001), .out(shifter_1_out));
  Multiplexer #(.select(2), .width(8), .enable("false")) multiplexer_1 (
    .in0(adder_1_out), .in1(and_1_out), .in2(shifter_1_out), .in3({8{1'b0}}), .out(multiplexer_1_out),
    .sel(FunCode));
  BitAdder bitadder_1 (.in0(multiplexer_1_out), .out(bitadder_1_out));
  assign Output = E_ALU ? multiplexer_1_out : 8'bz;  // Controlled_Buffer controlled_buffer_1
  Comparator #(.width(4)) comparator_1 (.a(bitadder_1_out), .b(4'b0000), .eq(comparator_1_eq));  // open: gt, lt
  Register #(.width(1), .trigger("high")) register_3 (.D(comparator_1_eq), .Q(z), .clk(C_ALU));  // open: en, clr

  // Notes on the sheet:
  //   0 ADD
  //   1 AND
  //   2 SHL
endmodule

module sub (
  input  [2:0] OPCODE,
  input  CLK,
  input  C_RESET,
  output S0_7,
  output S1_7,
  output S2_7,
  output S3_7,
  output S0_6,
  output S1_6,
  output S2_6,
  output S3_6,
  output S0_5,
  output S1_5,
  output S2_5,
  output S3_5,
  output S0_4,
  output S1_4,
  output S2_4,
  output S3_4,
  output S0_3,
  output S1_3,
  output S2_3,
  output S3_3,
  output S0_2,
  output S1_2,
  output S2_2,
  output S3_2,
  output S0_1,
  output S1_1,
  output S2_1,
  output S3_1,
  output S0_0,
  output S1_0,
  output S2_0,
  output S3_0,
  output S4_7,
  output S5_7,
  output S6_7,
  output S7_7,
  output S4_6,
  output S5_6,
  output S6_6,
  output S7_6,
  output S4_5,
  output S5_5,
  output S6_5,
  output S7_5,
  output S4_4,
  output S5_4,
  output S6_4,
  output S7_4,
  output S4_3,
  output S5_3,
  output S6_3,
  output S7_3,
  output S4_2,
  output S5_2,
  output S6_2,
  output S7_2,
  output S4_1,
  output S5_1,
  output S6_1,
  output S7_1,
  output S4_0,
  output S5_0,
  output S6_0,
  output S7_0
);

  wire decoder_1_out0, decoder_1_out1, decoder_1_out2, decoder_1_out3, decoder_1_out4, decoder_1_out5,
       decoder_1_out6, decoder_1_out7;
  wire [2:0] counter_1_q;

  Counter #(.width(3), .max('h7)) counter_1 (.Q(counter_1_q), .clk(CLK), .clr(C_RESET));  // open: load, D, count, carry
  Decoder #(.select(3), .enable("false")) decoder_1 (
    .out0(decoder_1_out0), .out1(decoder_1_out1), .out2(decoder_1_out2), .out3(decoder_1_out3),
    .out4(decoder_1_out4), .out5(decoder_1_out5), .out6(decoder_1_out6), .out7(decoder_1_out7),
    .sel(counter_1_q));
  Decoder #(.select(3), .disabled(0)) decoder_2 (
    .out0(S0_0), .out1(S0_1), .out2(S0_2), .out3(S0_3), .out4(S0_4), .out5(S0_5), .out6(S0_6), .out7(S0_7),
    .sel(OPCODE), .en(decoder_1_out0));
  Decoder #(.select(3), .disabled(0)) decoder_3 (
    .out0(S4_0), .out1(S4_1), .out2(S4_2), .out3(S4_3), .out4(S4_4), .out5(S4_5), .out6(S4_6), .out7(S4_7),
    .sel(OPCODE), .en(decoder_1_out4));
  Decoder #(.select(3), .disabled(0)) decoder_4 (
    .out0(S1_0), .out1(S1_1), .out2(S1_2), .out3(S1_3), .out4(S1_4), .out5(S1_5), .out6(S1_6), .out7(S1_7),
    .sel(OPCODE), .en(decoder_1_out1));
  Decoder #(.select(3), .disabled(0)) decoder_5 (
    .out0(S5_0), .out1(S5_1), .out2(S5_2), .out3(S5_3), .out4(S5_4), .out5(S5_5), .out6(S5_6), .out7(S5_7),
    .sel(OPCODE), .en(decoder_1_out5));
  Decoder #(.select(3), .disabled(0)) decoder_6 (
    .out0(S2_0), .out1(S2_1), .out2(S2_2), .out3(S2_3), .out4(S2_4), .out5(S2_5), .out6(S2_6), .out7(S2_7),
    .sel(OPCODE), .en(decoder_1_out2));
  Decoder #(.select(3), .disabled(0)) decoder_7 (
    .out0(S6_0), .out1(S6_1), .out2(S6_2), .out3(S6_3), .out4(S6_4), .out5(S6_5), .out6(S6_6), .out7(S6_7),
    .sel(OPCODE), .en(decoder_1_out6));
  Decoder #(.select(3), .disabled(0)) decoder_8 (
    .out0(S3_0), .out1(S3_1), .out2(S3_2), .out3(S3_3), .out4(S3_4), .out5(S3_5), .out6(S3_6), .out7(S3_7),
    .sel(OPCODE), .en(decoder_1_out3));
  Decoder #(.select(3), .disabled(0)) decoder_9 (
    .out0(S7_0), .out1(S7_1), .out2(S7_2), .out3(S7_3), .out4(S7_4), .out5(S7_5), .out6(S7_6), .out7(S7_7),
    .sel(OPCODE), .en(decoder_1_out7));

  // Notes on the sheet:
  //   SUB_0
  //   SUB_4
  //   SUB_1
  //   SUB_5
  //   SUB_2
  //   SUB_6
  //   SUB_3
  //   SUB_7
endmodule

module control (
  input  z,
  input  CLOCK,
  input  [2:0] OPCODE,
  output E_PC,
  output C_MAR,
  output C_IR,
  output E_MEM,
  output INC_PC,
  output C_PC,
  output E_IR,
  output C_MBR,
  output C_D0,
  output E_D0,
  output C_MEM,
  output C_ALU,
  output E_ALU,
  output C_BCD
);

  wire and_1_out, or_3_out, or_4_out, or_5_out, or_8_out, or_9_out, or_10_out, or_11_out, or_20_out,
       sub_1_s0_0, sub_1_s0_1, sub_1_s0_2, sub_1_s0_3, sub_1_s0_4, sub_1_s0_5, sub_1_s0_6, sub_1_s0_7,
       sub_1_s1_0, sub_1_s1_1, sub_1_s1_2, sub_1_s1_3, sub_1_s1_4, sub_1_s1_5, sub_1_s1_6, sub_1_s1_7,
       sub_1_s2_0, sub_1_s2_1, sub_1_s2_2, sub_1_s2_3, sub_1_s2_4, sub_1_s2_5, sub_1_s2_6, sub_1_s2_7,
       sub_1_s3_0, sub_1_s3_1, sub_1_s3_2, sub_1_s3_3, sub_1_s3_4, sub_1_s3_5, sub_1_s3_6, sub_1_s3_7,
       sub_1_s4_0, sub_1_s4_1, sub_1_s4_2, sub_1_s4_3, sub_1_s4_4, sub_1_s4_6, sub_1_s4_7, sub_1_s5_0,
       sub_1_s5_1, sub_1_s5_2, sub_1_s5_4, sub_1_s5_5, sub_1_s5_6, sub_1_s5_7, sub_1_s6_0, sub_1_s6_1,
       sub_1_s6_2, sub_1_s6_3, sub_1_s6_4, sub_1_s6_5, sub_1_s6_6, sub_1_s6_7, sub_1_s7_0, sub_1_s7_1,
       sub_1_s7_2, sub_1_s7_3, sub_1_s7_4, sub_1_s7_5, sub_1_s7_6, sub_1_s7_7;

  or or_1 (E_PC, sub_1_s0_0, sub_1_s0_1, sub_1_s0_2, sub_1_s0_3, sub_1_s0_4, sub_1_s0_5, sub_1_s0_6, sub_1_s0_7);
  or or_2 (C_IR, sub_1_s1_0, sub_1_s1_1, sub_1_s1_2, sub_1_s1_3, sub_1_s1_4, sub_1_s1_5, sub_1_s1_6, sub_1_s1_7);
  or or_3 (or_3_out, sub_1_s2_0, sub_1_s2_1, sub_1_s2_2, sub_1_s2_3, sub_1_s2_4, sub_1_s2_5, sub_1_s2_6, sub_1_s2_7);
  or or_4 (or_4_out, sub_1_s3_6, sub_1_s3_7);
  or or_5 (or_5_out, sub_1_s3_0, sub_1_s3_1, sub_1_s3_2, sub_1_s3_3, sub_1_s3_4, sub_1_s3_5);
  or or_6 (C_MBR, sub_1_s4_0, sub_1_s4_1, sub_1_s4_2, sub_1_s4_3);
  or or_7 (C_ALU, sub_1_s5_0, sub_1_s5_1, sub_1_s5_2);
  or or_8 (or_8_out, sub_1_s5_4, sub_1_s5_5, sub_1_s5_6, sub_1_s5_7);
  or or_9 (or_9_out, sub_1_s6_0, sub_1_s6_1);
  or or_10 (or_10_out, sub_1_s6_3, sub_1_s6_4, sub_1_s6_5, sub_1_s6_6, sub_1_s6_7);
  and and_1 (and_1_out, sub_1_s4_7, z);
  or or_11 (or_11_out, sub_1_s7_0, sub_1_s7_1, sub_1_s7_2, sub_1_s7_3, sub_1_s7_4, sub_1_s7_5, sub_1_s7_6, sub_1_s7_7);
  sub sub_1 (
    .OPCODE(OPCODE), .S0_0(sub_1_s0_0), .S4_0(sub_1_s4_0), .S0_1(sub_1_s0_1), .S4_1(sub_1_s4_1),
    .S0_2(sub_1_s0_2), .S4_2(sub_1_s4_2), .S0_3(sub_1_s0_3), .S4_3(sub_1_s4_3), .S0_4(sub_1_s0_4),
    .S4_4(sub_1_s4_4), .S0_5(sub_1_s0_5), .S4_5(E_D0), .S0_6(sub_1_s0_6), .S4_6(sub_1_s4_6),
    .S0_7(sub_1_s0_7), .S4_7(sub_1_s4_7), .S1_0(sub_1_s1_0), .S5_0(sub_1_s5_0), .S1_1(sub_1_s1_1),
    .S5_1(sub_1_s5_1), .S1_2(sub_1_s1_2), .S5_2(sub_1_s5_2), .S1_3(sub_1_s1_3), .S5_3(C_BCD),
    .S1_4(sub_1_s1_4), .S5_4(sub_1_s5_4), .S1_5(sub_1_s1_5), .S5_5(sub_1_s5_5), .S1_6(sub_1_s1_6),
    .S5_6(sub_1_s5_6), .S1_7(sub_1_s1_7), .S5_7(sub_1_s5_7), .S2_0(sub_1_s2_0), .S6_0(sub_1_s6_0),
    .S2_1(sub_1_s2_1), .S6_1(sub_1_s6_1), .S2_2(sub_1_s2_2), .S6_2(sub_1_s6_2), .S2_3(sub_1_s2_3),
    .S6_3(sub_1_s6_3), .S2_4(sub_1_s2_4), .S6_4(sub_1_s6_4), .S2_5(sub_1_s2_5), .S6_5(sub_1_s6_5),
    .S2_6(sub_1_s2_6), .S6_6(sub_1_s6_6), .S2_7(sub_1_s2_7), .S6_7(sub_1_s6_7), .S3_0(sub_1_s3_0),
    .S7_0(sub_1_s7_0), .S3_1(sub_1_s3_1), .S7_1(sub_1_s7_1), .S3_2(sub_1_s3_2), .S7_2(sub_1_s7_2),
    .S3_3(sub_1_s3_3), .S7_3(sub_1_s7_3), .S3_4(sub_1_s3_4), .S7_4(sub_1_s7_4), .S3_5(sub_1_s3_5),
    .S7_5(sub_1_s7_5), .S3_6(sub_1_s3_6), .S7_6(sub_1_s7_6), .S3_7(sub_1_s3_7), .S7_7(sub_1_s7_7),
    .CLK(CLOCK), .C_RESET(or_20_out));
  or or_12 (C_MAR, E_PC, or_5_out);
  or or_13 (E_MEM, C_IR, C_MBR, sub_1_s4_4);
  or or_14 (INC_PC, C_IR, or_3_out);
  or or_15 (C_PC, or_3_out, sub_1_s4_6, and_1_out);
  or or_16 (E_IR, or_4_out, or_5_out, sub_1_s4_6, sub_1_s4_7);
  or or_17 (C_D0, sub_1_s4_4, or_9_out);
  or or_18 (C_MEM, E_D0, sub_1_s6_2);
  or or_19 (E_ALU, C_ALU, or_9_out, sub_1_s6_2);
  or or_20 (or_20_out, or_11_out, or_10_out, or_8_out);

  // Notes on the sheet:
  //   CLK_RESET
endmodule

module cpu (
);

  wire C_ALU, C_BCD, C_D0, C_IR, C_MAR, C_MBR, C_MEM, C_PC, CLOCK_out, E_ALU, E_D0, E_IR, E_MEM, E_PC,
       h2bcd_1_sign, INC_PC, Z;
  wire [2:0] OPCODE;
  wire [3:0] adder_1_out, controlled_buffer_1_out, h2bcd_1_hundred, h2bcd_1_single, h2bcd_1_ten, MAR_q,
       multiplexer_1_out, PC_q;
  wire [7:0] BCD_q, controlled_buffer_2_out, D0_q, IR_q, MBR_q, ram_1_data;

  Adder #(.width(4)) adder_1 (.a(PC_q), .b(4'b0001), .out(adder_1_out));  // open: cin, cout
  Clock CLOCK (.out(CLOCK_out));
  Multiplexer #(.width(4), .enable("false")) multiplexer_1 (
    .in0(controlled_buffer_1_out), .in1(adder_1_out), .out(multiplexer_1_out), .sel(INC_PC));
  Register #(.width(4)) PC (.D(multiplexer_1_out), .Q(PC_q), .clk(C_PC));  // open: en, clr
  assign controlled_buffer_1_out = E_PC ? PC_q : 4'bz;  // Controlled_Buffer controlled_buffer_1
  Register #(.width(4), .trigger("high")) MAR (.D(controlled_buffer_1_out), .Q(MAR_q), .clk(C_MAR));  // open: en, clr
  control control_1 (
    .z(Z), .CLOCK(CLOCK_out), .E_PC(E_PC), .C_MAR(C_MAR), .C_IR(C_IR), .E_MEM(E_MEM), .INC_PC(INC_PC),
    .C_PC(C_PC), .E_IR(E_IR), .C_MBR(C_MBR), .C_D0(C_D0), .E_D0(E_D0), .C_MEM(C_MEM), .C_ALU(C_ALU),
    .E_ALU(E_ALU), .OPCODE(OPCODE), .C_BCD(C_BCD));
  assign controlled_buffer_2_out = E_MEM ? ram_1_data : 8'bz;  // Controlled_Buffer controlled_buffer_2
  RAM #(.addrWidth(4), .bus("separate")) ram_1 (
    .addr(MAR_q), .din(controlled_buffer_2_out), .data(ram_1_data), .clk(C_MEM));  // open: str, sel, ld, clr
  Register #(.trigger("high")) MBR (.D(controlled_buffer_2_out), .Q(MBR_q), .clk(C_MBR));  // open: en, clr
  Register #(.trigger("high")) D0 (.D(controlled_buffer_2_out), .Q(D0_q), .clk(C_D0));  // open: en, clr
  Register #(.trigger("high")) IR (
    .D(controlled_buffer_2_out), .Q({IR_q[7], OPCODE, IR_q[3:0]}), .clk(C_IR));  // open: en, clr
  _7_Segment_Display u_7_segment_display_1 (.g(h2bcd_1_sign));  // open: f, a, b, e, d, c, dp
  Register #(.trigger("high")) BCD (.D(MBR_q), .Q(BCD_q), .clk(C_BCD));  // open: en, clr
  assign controlled_buffer_2_out = E_D0 ? D0_q : 8'bz;  // Controlled_Buffer controlled_buffer_3
  assign controlled_buffer_1_out = E_IR ? IR_q[3:0] : 4'bz;  // Controlled_Buffer controlled_buffer_4
  Hex_Digit_Display hex_digit_display_1 (.value(h2bcd_1_hundred));  // open: dp
  h2bcd h2bcd_1 (
    .\input (BCD_q), .hundred(h2bcd_1_hundred), .ten(h2bcd_1_ten), .single(h2bcd_1_single),
    .Sign(h2bcd_1_sign));
  Hex_Digit_Display hex_digit_display_2 (.value(h2bcd_1_ten));  // open: dp
  Hex_Digit_Display hex_digit_display_3 (.value(h2bcd_1_single));  // open: dp
  alu alu_1 (
    .Input_1(MBR_q), .Input_2(D0_q), .Output(controlled_buffer_2_out), .E_ALU(E_ALU), .z(Z),
    .FunCode(OPCODE[1:0]), .C_ALU(C_ALU));

  // Notes on the sheet:
  //   PC+1
  //   n/PC+1
  //   E_PC
  //   (MDR)
  //   MEM
  //   E_MEM
  //   C_IR
  //   BUS
  //   OPERAND0-3
  //   E_D0(MDR)
  //   OPCODE4-6
  //   E_IR
  //   z
endmodule

module microcode (
  input  z,
  input  [2:0] OPCODE,
  input  CLOCK,
  output E_PC,
  output C_MAR,
  output C_IR,
  output E_MEM,
  output INC_PC,
  output C_PC,
  output E_IR,
  output C_MBR,
  output C_BCD,
  output C_D0,
  output E_D0,
  output C_MEM,
  output C_ALU,
  output E_ALU
);

  wire and_1_out;
  wire [2:0] counter_1_q;
  wire [15:5] rom_1_data;

  Counter #(.width(3), .max('h7)) counter_1 (
    .Q(counter_1_q), .clk(CLOCK), .clr(rom_1_data[15]));  // open: load, D, count, carry
  ROM #(.addrWidth(6), .dataWidth(16)) rom_1 (
    .addr({counter_1_q, OPCODE}),
    .data({rom_1_data[15], E_ALU, C_ALU, rom_1_data[12], E_D0, C_D0, C_BCD, C_MBR, E_IR, rom_1_data[6:5], INC_PC, E_MEM, C_IR, C_MAR, E_PC}));  // open: sel
  and and_1 (and_1_out, rom_1_data[6], z);
  or or_1 (C_PC, rom_1_data[5], and_1_out);
  buf buffer_1 (C_MEM, rom_1_data[12]);

  // Notes on the sheet:
  //   contents of rom_1 (hex, n*v repeats v):
  //   8*3 8*1c 8*30 6*82 80 80 4*108 408 1800 a0 c0 6000 6000 6000 200 4*8000 4400 4400 5000 13*8000
  //   CLK_RESET
endmodule

module cpu2 (
);

  wire C_ALU, C_BCD, C_D0, C_IR, C_MAR, C_MBR, C_MEM, C_PC, CLOCK_out, E_ALU, E_D0, E_IR, E_MEM, E_PC,
       h2bcd_1_sign, INC_PC, Z;
  wire [2:0] OPCODE;
  wire [3:0] adder_1_out, controlled_buffer_1_out, h2bcd_1_hundred, h2bcd_1_single, h2bcd_1_ten, MAR_q,
       multiplexer_1_out, PC_q;
  wire [7:0] BCD_q, controlled_buffer_2_out, D0_q, IR_q, MBR_q, ram_1_data;

  Adder #(.width(4)) adder_1 (.a(PC_q), .b(4'b0001), .out(adder_1_out));  // open: cin, cout
  Clock CLOCK (.out(CLOCK_out));
  Multiplexer #(.width(4), .enable("false")) multiplexer_1 (
    .in0(controlled_buffer_1_out), .in1(adder_1_out), .out(multiplexer_1_out), .sel(INC_PC));
  Register #(.width(4)) PC (.D(multiplexer_1_out), .Q(PC_q), .clk(C_PC));  // open: en, clr
  assign controlled_buffer_1_out = E_PC ? PC_q : 4'bz;  // Controlled_Buffer controlled_buffer_1
  Register #(.width(4), .trigger("high")) MAR (.D(controlled_buffer_1_out), .Q(MAR_q), .clk(C_MAR));  // open: en, clr
  microcode microcode_1 (
    .z(Z), .E_PC(E_PC), .C_MAR(C_MAR), .C_IR(C_IR), .E_MEM(E_MEM), .INC_PC(INC_PC), .C_PC(C_PC), .E_IR(E_IR),
    .C_MBR(C_MBR), .C_D0(C_D0), .E_D0(E_D0), .C_MEM(C_MEM), .C_ALU(C_ALU), .E_ALU(E_ALU), .CLOCK(CLOCK_out),
    .OPCODE(OPCODE), .C_BCD(C_BCD));
  assign controlled_buffer_2_out = E_MEM ? ram_1_data : 8'bz;  // Controlled_Buffer controlled_buffer_2
  RAM #(.addrWidth(4), .bus("separate")) ram_1 (
    .addr(MAR_q), .din(controlled_buffer_2_out), .data(ram_1_data), .clk(C_MEM));  // open: str, sel, ld, clr
  Register #(.trigger("high")) MBR (.D(controlled_buffer_2_out), .Q(MBR_q), .clk(C_MBR));  // open: en, clr
  Register #(.trigger("high")) D0 (.D(controlled_buffer_2_out), .Q(D0_q), .clk(C_D0));  // open: en, clr
  Register #(.trigger("high")) IR (
    .D(controlled_buffer_2_out), .Q({IR_q[7], OPCODE, IR_q[3:0]}), .clk(C_IR));  // open: en, clr
  _7_Segment_Display u_7_segment_display_1 (.g(h2bcd_1_sign));  // open: f, a, b, e, d, c, dp
  Register #(.trigger("high")) BCD (.D(MBR_q), .Q(BCD_q), .clk(C_BCD));  // open: en, clr
  assign controlled_buffer_2_out = E_D0 ? D0_q : 8'bz;  // Controlled_Buffer controlled_buffer_3
  assign controlled_buffer_1_out = E_IR ? IR_q[3:0] : 4'bz;  // Controlled_Buffer controlled_buffer_4
  Hex_Digit_Display hex_digit_display_1 (.value(h2bcd_1_hundred));  // open: dp
  h2bcd h2bcd_1 (
    .\input (BCD_q), .hundred(h2bcd_1_hundred), .ten(h2bcd_1_ten), .single(h2bcd_1_single),
    .Sign(h2bcd_1_sign));
  Hex_Digit_Display hex_digit_display_2 (.value(h2bcd_1_single));  // open: dp
  Hex_Digit_Display hex_digit_display_3 (.value(h2bcd_1_ten));  // open: dp
  alu alu_1 (
    .Input_1(MBR_q), .Input_2(D0_q), .Output(controlled_buffer_2_out), .E_ALU(E_ALU), .z(Z),
    .FunCode(OPCODE[1:0]), .C_ALU(C_ALU));

  // Notes on the sheet:
  //   PC+1
  //   n/PC+1
  //   E_PC
  //   (MDR)
  //   MEM
  //   E_MEM
  //   C_IR
  //   BUS
  //   OPERAND0-3
  //   E_D0(MDR)
  //   OPCODE4-6
  //   E_IR
  //   z
endmodule

module cpu3 (
);

  wire C_ALU, C_BCD, C_D0, C_IR, C_MAR, C_MBR, C_MEM, C_PC, CLOCK_out, E_ALU, E_D0, E_IR, E_MEM, E_PC,
       h2bcd_1_sign, INC_PC, Z;
  wire [1:0] ir_parsing_1_out_3;
  wire [2:0] OPCODE;
  wire [3:0] controlled_buffer_1_out, h2bcd_1_hundred, h2bcd_1_single, h2bcd_1_ten, ir_parsing_1_out_4,
       MAR_q, multiplexer_1_out, pc_1_1_out_2, PC_q;
  wire [7:0] ALU_1, ALU_2, BCD_q, controlled_buffer_2_out, IR_q, ram_1_data;

  Clock CLOCK (.out(CLOCK_out));
  Multiplexer #(.width(4), .enable("false")) multiplexer_1 (
    .in0(controlled_buffer_1_out), .in1(pc_1_1_out_2), .out(multiplexer_1_out), .sel(INC_PC));
  Register #(.width(4)) PC (.D(multiplexer_1_out), .Q(PC_q), .clk(C_PC));  // open: en, clr
  PC_1 pc_1_1 (.PC_1(PC_q), .out_2(pc_1_1_out_2));
  assign controlled_buffer_1_out = E_PC ? PC_q : 4'bz;  // Controlled_Buffer controlled_buffer_1
  Register #(.width(4), .trigger("high")) MAR (.D(controlled_buffer_1_out), .Q(MAR_q), .clk(C_MAR));  // open: en, clr
  microcode microcode_1 (
    .z(Z), .E_PC(E_PC), .C_MAR(C_MAR), .C_IR(C_IR), .E_MEM(E_MEM), .INC_PC(INC_PC), .C_PC(C_PC), .E_IR(E_IR),
    .C_MBR(C_MBR), .C_D0(C_D0), .E_D0(E_D0), .C_MEM(C_MEM), .C_ALU(C_ALU), .E_ALU(E_ALU), .CLOCK(CLOCK_out),
    .OPCODE(OPCODE), .C_BCD(C_BCD));
  assign controlled_buffer_2_out = E_MEM ? ram_1_data : 8'bz;  // Controlled_Buffer controlled_buffer_2
  RAM #(.addrWidth(4), .bus("separate")) ram_1 (
    .addr(MAR_q), .din(controlled_buffer_2_out), .data(ram_1_data), .clk(C_MEM));  // open: str, sel, ld, clr
  Register #(.trigger("high")) MBR (.D(controlled_buffer_2_out), .Q(ALU_1), .clk(C_MBR));  // open: en, clr
  Register #(.trigger("high")) D0 (.D(controlled_buffer_2_out), .Q(ALU_2), .clk(C_D0));  // open: en, clr
  Register #(.trigger("high")) IR (.D(controlled_buffer_2_out), .Q(IR_q), .clk(C_IR));  // open: en, clr
  Register #(.trigger("high")) BCD (.D(ALU_1), .Q(BCD_q), .clk(C_BCD));  // open: en, clr
  assign controlled_buffer_2_out = E_D0 ? ALU_2 : 8'bz;  // Controlled_Buffer controlled_buffer_3
  IR_Parsing ir_parsing_1 (.in_2(IR_q), .out_3(ir_parsing_1_out_3), .out_4(ir_parsing_1_out_4), .in_1(OPCODE));
  _7_Segment_Display u_7_segment_display_1 (.g(h2bcd_1_sign));  // open: f, a, b, e, d, c, dp
  h2bcd h2bcd_1 (
    .\input (BCD_q), .hundred(h2bcd_1_hundred), .ten(h2bcd_1_ten), .single(h2bcd_1_single),
    .Sign(h2bcd_1_sign));
  assign controlled_buffer_1_out = E_IR ? ir_parsing_1_out_4 : 4'bz;  // Controlled_Buffer controlled_buffer_4
  Hex_Digit_Display hex_digit_display_1 (.value(h2bcd_1_ten));  // open: dp
  Hex_Digit_Display hex_digit_display_2 (.value(h2bcd_1_hundred));  // open: dp
  alu u_alu_1 (
    .Input_1(ALU_1), .Input_2(ALU_2), .Output(controlled_buffer_2_out), .E_ALU(E_ALU), .z(Z),
    .FunCode(ir_parsing_1_out_3), .C_ALU(C_ALU));
  Hex_Digit_Display hex_digit_display_3 (.value(h2bcd_1_single));  // open: dp

  // Notes on the sheet:
  //   n/PC+1
  //   E_PC
  //   MEM
  //   BUS
  //   E_MEM
  //   OPCODE4-6
  //   OPERAND0-3
  //   E_D0(MDR)
endmodule

module PC_1 (
  input  [3:0] PC_1,
  output [3:0] out_2
);

  Adder #(.width(4)) adder_1 (.a(PC_1), .b(4'b0001), .out(out_2));  // open: cin, cout
endmodule

module IR_Parsing (
  input  [2:0] in_1,
  input  [7:0] in_2,
  output [1:0] out_3,
  output [3:0] out_4
);


  assign in_2[6:4] = in_1;
  assign out_3 = in_1[1:0];
  assign out_4 = in_2[3:0];
endmodule
