// Logisim project 3bit_DownCounter_TFlipFlop.circ as structural Verilog: 1 circuit, main circuit main
module main (
  input  in_1
);

  wire and_1_out, and_2_out, clock_1_out, T0_qn, T1_qn;
  wire [2:0] T0_q;

  Clock clock_1 (.out(clock_1_out));
  and and_1 (and_1_out, T0_qn, in_1);
  and and_2 (and_2_out, and_1_out, T1_qn);
  T_Flip_Flop T0 (.clk(clock_1_out), .T(in_1), .Q(T0_q[0]), .Qn(T0_qn));  // open: preset, reset, en
  T_Flip_Flop T1 (.clk(clock_1_out), .T(and_1_out), .Q(T0_q[1]), .Qn(T1_qn));  // open: preset, reset, en
  T_Flip_Flop T2 (.clk(clock_1_out), .T(and_2_out), .Q(T0_q[2]));  // open: Qn, preset, reset, en
  Hex_Digit_Display hex_digit_display_1 (.value({1'b0, T0_q}));  // open: dp
endmodule
