// Logisim project 4bitBCDReverse.circ as structural Verilog: 1 circuit, main circuit main
module main (
);

  wire and_1_out, and_2_out, and_3_out, and_4_out, and_5_out, and_6_out, clock_1_out, or_1_out, or_2_out,
       T0_qn, T1_qn, T2_qn, T3_qn;
  wire [3:0] T0_q;

  Clock clock_1 (.out(clock_1_out));
  and and_1 (and_1_out, T0_q[1], T0_qn);
  and and_2 (and_2_out, T0_q[3], T0_qn);
  and and_3 (and_3_out, T0_q[2], T0_qn, T1_qn);
  and and_4 (and_4_out, T0_q[3], T1_qn, T0_qn);
  and and_5 (and_5_out, T0_q[2], T1_qn, T0_qn);
  and and_6 (and_6_out, T2_qn, T1_qn, T0_qn);
  or or_1 (or_1_out, and_2_out, and_3_out);
  or or_2 (or_2_out, and_4_out, and_5_out, and_1_out);
  T_Flip_Flop T3 (.clk(clock_1_out), .T(and_6_out), .Q(T0_q[3]), .Qn(T3_qn));  // open: preset, reset, en
  T_Flip_Flop T2 (.clk(clock_1_out), .T(or_1_out), .Q(T0_q[2]), .Qn(T2_qn));  // open: preset, reset, en
  T_Flip_Flop T1 (.clk(clock_1_out), .T(or_2_out), .Q(T0_q[1]), .Qn(T1_qn));  // open: preset, reset, en
  T_Flip_Flop T0 (.clk(clock_1_out), .T(1'b1), .Q(T0_q[0]), .Qn(T0_qn));  // open: preset, reset, en
  Hex_Digit_Display hex_digit_display_1 (.value(T0_q));  // open: dp
endmodule
