// Logisim project 4bitBCDUpCounter_TFlipFlop.circ as structural Verilog: 1 circuit, main circuit main
module main (
);

  wire and_1_out, and_2_out, and_3_out, and_4_out, clock_1_out, or_1_out, T3_qn;
  wire [3:0] T0_q;

  Clock clock_1 (.out(clock_1_out));
  and and_1 (and_1_out, T0_q[3], T0_q[0]);
  and and_2 (and_2_out, T0_q[0], T0_q[1], T0_q[2]);
  and and_3 (and_3_out, T3_qn, T0_q[0]);
  T_Flip_Flop T3 (.clk(clock_1_out), .T(or_1_out), .Q(T0_q[3]), .Qn(T3_qn));  // open: preset, reset, en
  or or_1 (or_1_out, and_1_out, and_2_out);
  T_Flip_Flop T2 (.clk(clock_1_out), .T(and_4_out), .Q(T0_q[2]));  // open: Qn, preset, reset, en
  and and_4 (and_4_out, T0_q[0], T0_q[1]);
  T_Flip_Flop T1 (.clk(clock_1_out), .T(and_3_out), .Q(T0_q[1]));  // open: Qn, preset, reset, en
  T_Flip_Flop T0 (.clk(clock_1_out), .T(1'b1), .Q(T0_q[0]));  // open: Qn, preset, reset, en
  Hex_Digit_Display hex_digit_display_1 (.value(T0_q));  // open: dp
endmodule
