// Logisim project 4bitEnable_DownCounter_JK.circ as structural Verilog: 1 circuit, main circuit main
module main (
  input  in_1
);

  wire and_1_out, and_2_out, and_3_out, clock_1_out, y0_qn, y1_qn, y2_qn;
  wire [3:0] y0_q;

  Clock clock_1 (.out(clock_1_out));
  and and_1 (and_1_out, in_1, y0_qn, y1_qn, y2_qn);
  and and_2 (and_2_out, in_1, y0_qn, y1_qn);
  and and_3 (and_3_out, in_1, y0_qn);
  J_K_Flip_Flop y3 (.J(and_1_out), .clk(clock_1_out), .K(and_1_out), .Q(y0_q[3]));  // open: Qn, preset, en, reset
  J_K_Flip_Flop y2 (
    .J(and_2_out), .clk(clock_1_out), .K(and_2_out), .Q(y0_q[2]), .Qn(y2_qn));  // open: preset, en, reset
  J_K_Flip_Flop y1 (
    .J(and_3_out), .clk(clock_1_out), .K(and_3_out), .Q(y0_q[1]), .Qn(y1_qn));  // open: preset, en, reset
  J_K_Flip_Flop y0 (.J(in_1), .clk(clock_1_out), .K(in_1), .Q(y0_q[0]), .Qn(y0_qn));  // open: preset, en, reset
  Hex_Digit_Display hex_digit_display_1 (.value(y0_q));  // open: dp
endmodule
