// Logisim project LabEx7.circ as structural Verilog: 3 circuits, main circuit main
module main (
  input  [4:0] \input 
);

  _7_Segment_Display u_7_segment_display_1 (.g(\input [4]));  // open: f, a, b, e, d, c, dp
  Hex_Digit_Display hex_digit_display_1 (.value(\input [3:0]));  // open: dp
endmodule

module _5bit_sign_magnitude (
  input  [4:0] \input ,
  output sign,
  output [3:0] Hex
);

  _7_Segment_Display u_7_segment_display_1 (.g(\input [4]));  // open: f, a, b, e, d, c, dp
  Hex_Digit_Display hex_digit_display_1 (.value(\input [3:0]));  // open: dp

  assign Hex = \input [3:0];
  assign sign = \input [4];
endmodule

module _5bit_2comp (
  input  [4:0] \input ,
  output [4:0] \output 
);

  wire [4:0] adder_1_out, not_1_out;

  assign not_1_out = ~\input ;  // NOT_Gate not_1, 5 bits wide
  Adder #(.width(5)) adder_1 (.a(not_1_out), .b(5'b00001), .out(adder_1_out), .cin(1'b0));  // open: cout
  _7_Segment_Display u_7_segment_display_1 (.g(\input [4]));  // open: f, a, b, e, d, c, dp
  Hex_Digit_Display hex_digit_display_1 (.value(\output [3:0]));  // open: dp
  Multiplexer #(.width(5), .enable("false")) multiplexer_1 (
    .in0(\input ), .in1(adder_1_out), .out(\output ), .sel(\input [4]));
endmodule
