// Logisim project MultiplexDisplayNotes.circ as structural Verilog: 1 circuit, main circuit main
module main (
  input  [3:0] in_1
);

  wire [3:0] multiplexer_1_out;

  Hex_Digit_Display hex_digit_display_1 (.value(multiplexer_1_out));  // open: dp
  Multiplexer #(.width(4), .enable("false")) multiplexer_1 (
    .in0(4'b1110), .in1(4'b0000), .out(multiplexer_1_out), .sel(in_1[0]));
endmodule
