// Logisim project TinyCPU12.circ as structural Verilog: 3 circuits, main circuit main
module main (
);

  wire alu_1_z, and_1_out, CLOCK_out, decoder_1_out0, decoder_1_out1, decoder_1_out2, decoder_1_out3,
       decoder_1_out4, decoder_1_out5, decoder_1_out6, decoder_1_out7, decoder_2_out0, decoder_2_out1,
       decoder_2_out2, decoder_2_out3, decoder_2_out4, decoder_2_out5, decoder_2_out6, decoder_2_out7,
       decoder_3_out0, decoder_3_out1, decoder_3_out2, decoder_3_out3, decoder_3_out4, decoder_3_out5,
       decoder_3_out6, decoder_3_out7, decoder_4_out0, decoder_4_out1, decoder_4_out2, decoder_4_out3,
       decoder_4_out4, decoder_4_out5, decoder_4_out6, decoder_4_out7, decoder_5_out0, decoder_5_out1,
       decoder_5_out2, decoder_5_out3, h2bcd_1_sign, or_1_out, or_2_out, or_3_out, or_4_out, or_5_out,
       or_6_out, or_7_out, or_8_out, or_9_out, or_10_out, or_11_out, or_12_out, or_13_out, or_14_out,
       or_15_out;
  wire [2:0] CYCLE_q, IR_q_2;
  wire [3:0] h2bcd_1_hundred, h2bcd_1_single, h2bcd_1_ten, h2bcd_1_thousand;
  wire [7:0] adder_1_out, controlled_buffer_1_out, MAR_q, multiplexer_1_out, PC_q;
  wire [11:0] BCD_q, controlled_buffer_2_out, D0_q, IR_q, MBR_q, ram_1_data;

  Clock CLOCK (.out(CLOCK_out));
  Adder adder_1 (.a(PC_q), .b(8'h1), .out(adder_1_out));  // open: cin, cout
  Decoder #(.select(3), .enable("false")) decoder_1 (
    .out0(decoder_1_out0), .out1(decoder_1_out1), .out2(decoder_1_out2), .out3(decoder_1_out3),
    .out4(decoder_1_out4), .out5(decoder_1_out5), .out6(decoder_1_out6), .out7(decoder_1_out7), .sel(CYCLE_q));
  Counter #(.width(3), .max('h7)) CYCLE (.Q(CYCLE_q), .clk(CLOCK_out), .clr(or_1_out));  // open: load, D, count, carry
  or or_1 (or_1_out, or_7_out, decoder_5_out3, decoder_1_out7);
  Multiplexer #(.width(8), .enable("false")) multiplexer_1 (
    .in0(controlled_buffer_1_out), .in1(adder_1_out), .out(multiplexer_1_out), .sel(or_2_out));
  or or_2 (or_2_out, decoder_1_out1, decoder_1_out2);
  Decoder #(.select(3), .disabled(0)) decoder_2 (
    .out0(decoder_2_out0), .out1(decoder_2_out1), .out2(decoder_2_out2), .out3(decoder_2_out3),
    .out4(decoder_2_out4), .out5(decoder_2_out5), .out6(decoder_2_out6), .out7(decoder_2_out7), .sel(IR_q_2),
    .en(decoder_1_out3));
  Decoder #(.select(3), .disabled(0)) decoder_3 (
    .out0(decoder_3_out0), .out1(decoder_3_out1), .out2(decoder_3_out2), .out3(decoder_3_out3),
    .out4(decoder_3_out4), .out5(decoder_3_out5), .out6(decoder_3_out6), .out7(decoder_3_out7), .sel(IR_q_2),
    .en(decoder_1_out5));
  Register PC (.D(multiplexer_1_out), .Q(PC_q), .clk(or_3_out));  // open: en, clr
  or or_3 (or_3_out, decoder_1_out2, and_1_out, decoder_4_out6);
  or or_4 (or_4_out, decoder_2_out0, decoder_2_out1, decoder_2_out2, decoder_2_out3, decoder_2_out4, decoder_2_out5);
  or or_5 (or_5_out, decoder_2_out6, decoder_2_out7);
  or or_6 (or_6_out, decoder_3_out0, decoder_3_out1, decoder_3_out2);
  or or_7 (or_7_out, decoder_3_out4, decoder_3_out5, decoder_3_out6, decoder_3_out7);
  assign controlled_buffer_1_out = decoder_1_out0 ? PC_q : 8'bz;  // Controlled_Buffer controlled_buffer_1
  or or_8 (or_8_out, decoder_1_out0, or_4_out);
  Decoder #(.select(3), .disabled(0)) decoder_4 (
    .out0(decoder_4_out0), .out1(decoder_4_out1), .out2(decoder_4_out2), .out3(decoder_4_out3),
    .out4(decoder_4_out4), .out5(decoder_4_out5), .out6(decoder_4_out6), .out7(decoder_4_out7), .sel(IR_q_2),
    .en(decoder_1_out4));
  Decoder #(.select(3), .disabled(0)) decoder_5 (
    .out0(decoder_5_out0), .out1(decoder_5_out1), .out2(decoder_5_out2), .out3(decoder_5_out3), .sel(IR_q_2),
    .en(decoder_1_out6));  // open: out4, out5, out6, out7
  Register #(.trigger("high")) MAR (.D(controlled_buffer_1_out), .Q(MAR_q), .clk(or_8_out));  // open: en, clr
  or or_9 (or_9_out, decoder_4_out0, decoder_4_out1, decoder_4_out2, decoder_4_out3);
  or or_10 (or_10_out, decoder_5_out0, decoder_5_out1);
  or or_11 (or_11_out, decoder_5_out2, decoder_4_out5);
  assign controlled_buffer_2_out = or_12_out ? ram_1_data : 12'bz;  // Controlled_Buffer controlled_buffer_2
  RAM #(.dataWidth(12), .bus("separate")) ram_1 (
    .addr(MAR_q), .din(controlled_buffer_2_out), .data(ram_1_data), .clk(or_11_out));  // open: str, sel, ld, clr
  or or_12 (or_12_out, decoder_1_out1, or_9_out, decoder_4_out4);
  Register #(.width(12), .trigger("high")) MBR (
    .D(controlled_buffer_2_out), .Q(MBR_q), .clk(or_9_out));  // open: en, clr
  and and_1 (and_1_out, decoder_4_out7, alu_1_z);
  Register #(.width(12), .trigger("high")) D0 (
    .D(controlled_buffer_2_out), .Q(D0_q), .clk(or_13_out));  // open: en, clr
  or or_13 (or_13_out, decoder_4_out4, or_10_out);
  Register #(.width(12), .trigger("high")) IR (
    .D(controlled_buffer_2_out), .Q({IR_q[11], IR_q_2, IR_q[7:0]}), .clk(decoder_1_out1));  // open: en, clr
  or or_14 (or_14_out, decoder_4_out7, decoder_4_out6, or_4_out, or_5_out);
  Register #(.width(12), .trigger("high")) BCD (.D(MBR_q), .Q(BCD_q), .clk(decoder_3_out3));  // open: en, clr
  assign controlled_buffer_2_out = decoder_4_out5 ? D0_q : 12'bz;  // Controlled_Buffer controlled_buffer_3
  assign controlled_buffer_1_out = or_14_out ? IR_q[7:0] : 8'bz;  // Controlled_Buffer controlled_buffer_4
  _7_Segment_Display u_7_segment_display_1 (.g(h2bcd_1_sign));  // open: f, a, b, e, d, c, dp
  Hex_Digit_Display hex_digit_display_1 (.value(h2bcd_1_thousand));  // open: dp
  h2bcd h2bcd_1 (
    .\input (BCD_q), .thousand(h2bcd_1_thousand), .hundred(h2bcd_1_hundred), .ten(h2bcd_1_ten),
    .single(h2bcd_1_single), .Sign(h2bcd_1_sign));
  Hex_Digit_Display hex_digit_display_2 (.value(h2bcd_1_ten));  // open: dp
  Hex_Digit_Display hex_digit_display_3 (.value(h2bcd_1_hundred));  // open: dp
  or or_15 (or_15_out, or_10_out, decoder_5_out2, or_6_out);
  Hex_Digit_Display hex_digit_display_4 (.value(h2bcd_1_single));  // open: dp
  alu alu_1 (
    .Input_1(MBR_q), .Input_2(D0_q), .Output(controlled_buffer_2_out), .E_ALU(or_15_out), .z(alu_1_z),
    .FunCode(IR_q_2[1:0]), .C_ALU(or_6_out));

  // Notes on the sheet:
  //   C_RESET
  //   PC+1
  //   INC_PC
  //   n/PC+1
  //   SUB_0
  //   SUB_2
  //   C_PC
  //   MAR<-IR0-3
  //   ALU<-MBR,D0
  //   HEX<-MBR
  //   E_PC
  //   C_MAR
  //   SUB_1
  //   SUB_3
  //   (MDR)
  //   MBR<-[MAR]
  //   PC<-IR0-3
  //   R0<-ALU
  //   MDR<-ALU
  //   MEM
  //   C_MEM
  //   D0<-[MAR]
  //   MDR<-D0
  //   E_MEM
  //   C_MBR
  //   BUS
  //   C_D0
  //   C_IR
  //   E_D0(MDR)
  //   OPCODE4-6
  //   E_IR
  //   OPERAND0-3
  //   C_BCD
  //   z
endmodule

// H2BCD
module h2bcd (
  input  [11:0] \input ,
  output [3:0] thousand,
  output [3:0] hundred,
  output [3:0] ten,
  output Sign,
  output [3:0] single
);

  wire [11:0] adder_1_out, divider_1_rem, divider_2_rem, multiplexer_1_out, not_1_out;
  wire [11:4] divider_1_out, divider_2_out, divider_3_out, divider_3_rem;

  assign not_1_out = ~\input ;  // NOT_Gate not_1, 12 bits wide
  Adder #(.width(12)) adder_1 (.a(not_1_out), .b(12'h1), .out(adder_1_out));  // open: cin, cout
  BitSelector #(.width(12)) bitselector_1 (.in(\input ), .out(Sign), .sel(4'b1011));
  Multiplexer #(.width(12)) multiplexer_1 (
    .in0(\input ), .in1(adder_1_out), .out(multiplexer_1_out), .sel(Sign));  // open: en
  Divider #(.width(12)) divider_1 (
    .a(multiplexer_1_out), .b(12'h3e8), .out({divider_1_out, thousand}), .rem(divider_1_rem));  // open: upper
  Divider #(.width(12)) divider_2 (
    .a(divider_1_rem), .b(12'h64), .out({divider_2_out, hundred}), .upper({12{1'b0}}), .rem(divider_2_rem));
  Divider #(.width(12)) divider_3 (
    .a(divider_2_rem), .b(12'ha), .out({divider_3_out, ten}), .upper({12{1'b0}}),
    .rem({divider_3_rem, single}));
endmodule

// ALU
module alu (
  input  [11:0] Input_1,
  input  [11:0] Input_2,
  input  E_ALU,
  input  [1:0] FunCode,
  input  C_ALU,
  output [11:0] Output,
  output z
);

  wire comparator_1_eq;
  wire [3:0] bitadder_1_out;
  wire [11:0] adder_1_out, and_1_out, controlled_buffer_1_out, controlled_buffer_2_out, multiplexer_1_out,
       shifter_1_out;

  assign controlled_buffer_1_out = C_ALU ? Input_1 : 12'bz;  // Controlled_Buffer controlled_buffer_1
  assign controlled_buffer_2_out = C_ALU ? Input_2 : 12'bz;  // Controlled_Buffer controlled_buffer_2
  Adder #(.width(12)) adder_1 (
    .a(controlled_buffer_1_out), .b(controlled_buffer_2_out), .out(adder_1_out));  // open: cin, cout
  assign and_1_out = controlled_buffer_1_out & controlled_buffer_2_out;  // AND_Gate and_1, 12 bits wide
  Shifter #(.width(12)) shifter_1 (.in(controlled_buffer_1_out), .\dist (4'b0001), .out(shifter_1_out));
  Multiplexer #(.select(2), .width(12), .enable("false")) multiplexer_1 (
    .in0(adder_1_out), .in1(and_1_out), .in2(shifter_1_out), .in3({12{1'b0}}), .out(multiplexer_1_out),
    .sel(FunCode));
  BitAdder #(.width(12)) bitadder_1 (.in0(multiplexer_1_out), .out(bitadder_1_out));
  assign Output = E_ALU ? multiplexer_1_out : 12'bz;  // Controlled_Buffer controlled_buffer_3
  Comparator #(.width(4)) comparator_1 (.a(bitadder_1_out), .b(4'b0000), .eq(comparator_1_eq));  // open: gt, lt
  Register #(.width(1), .trigger("high")) register_1 (.D(comparator_1_eq), .Q(z), .clk(C_ALU));  // open: en, clr

  // Notes on the sheet:
  //   0 ADD
  //   1 AND
  //   2 SHL
endmodule
